// Logisim project BCDtoDIGIT.circ as structural Verilog: 1 circuit, main circuit main
module main (
  input  in_1,
  input  in_2,
  input  in_3,
  input  in_4,
  output right_up,
  output up,
  output left_up,
  output mid,
  output leftdown,
  output down,
  output right_down
);

  wire _0_out, _1_out, _2_out, _3_out, _4_out, _5_out, _6_out, _7_out, _8_out, _9_out, not_1_out, not_2_out,
       not_3_out, not_4_out;

  not not_1 (not_1_out, in_1);
  not not_2 (not_2_out, in_2);
  not not_3 (not_3_out, in_3);
  not not_4 (not_4_out, in_4);
  and _1 (_1_out, in_4, not_3_out, not_2_out, not_1_out);
  and _2 (_2_out, not_4_out, in_3, not_2_out, not_1_out);
  and _3 (_3_out, in_4, in_3, not_2_out, not_1_out);
  and _4 (_4_out, not_4_out, not_3_out, in_2, not_1_out);
  and _5 (_5_out, in_4, not_3_out, in_2, not_1_out);
  and _6 (_6_out, not_4_out, in_3, in_2, not_1_out);
  and _7 (_7_out, in_4, in_3, in_2, not_1_out);
  and _8 (_8_out, not_4_out, not_3_out, not_2_out, in_1);
  and _9 (_9_out, in_4, not_3_out, not_2_out, in_1);
  and _0 (_0_out, not_4_out, not_3_out, not_2_out, not_1_out);
  or or_1 (right_up, _1_out, _2_out, _3_out, _4_out, _7_out, _8_out, _9_out, _0_out);
  or or_2 (up, _2_out, _3_out, _5_out, _6_out, _7_out, _8_out, _9_out, _0_out);
  or or_3 (left_up, _4_out, _5_out, _6_out, _8_out, _9_out, _0_out);
  or or_4 (mid, _2_out, _3_out, _4_out, _6_out, _5_out, _8_out, _9_out);
  or or_5 (leftdown, _2_out, _6_out, _8_out, _0_out);
  or or_6 (down, _8_out, _2_out, _3_out, _5_out, _6_out, _0_out);
  or or_7 (right_down, _1_out, _3_out, _4_out, _5_out, _0_out, _6_out, _7_out, _8_out, _9_out);
endmodule
