// Logisim project Disp.circ as structural Verilog: 6 circuits, main circuit main
module main (
  input  b7,
  input  in_2,
  input  in_3,
  input  in_4,
  input  in_5,
  input  in_6,
  input  in_7,
  input  b0,
  input  in_9
);

  wire Shift_1_to_3_o0, Shift_1_to_3_o8, Shift_1_to_3_out_11, Shift_1_to_3_out_12, Shift_1_to_3_out_13,
       Shift_1_to_3_out_14, Shift_1_to_3_out_15, Shift_1_to_3_out_17;

  Shift_1_3 Shift_1_to_3 (
    .b7(b7), .in_2(in_2), .in_3(in_3), .in_4(in_4), .in_5(in_5), .in_6(in_6), .in_7(in_7), .b0(b0),
    .ZERO(in_9), .O8(Shift_1_to_3_o8), .out_11(Shift_1_to_3_out_11), .out_12(Shift_1_to_3_out_12),
    .out_13(Shift_1_to_3_out_13), .out_14(Shift_1_to_3_out_14), .out_15(Shift_1_to_3_out_15),
    .out_16(Shift_1_to_3_out_15), .out_17(Shift_1_to_3_out_17), .O0(Shift_1_to_3_o0));
  shift_4 shift_4_1 (
    .b8(Shift_1_to_3_o8), .in_2(Shift_1_to_3_out_11), .in_3(Shift_1_to_3_out_12), .in_4(Shift_1_to_3_out_13),
    .in_5(Shift_1_to_3_out_14), .in_6(Shift_1_to_3_out_15), .in_7(Shift_1_to_3_out_15),
    .in_8(Shift_1_to_3_out_17), .b0(Shift_1_to_3_o0), .ZERO(in_9));  // open: O9, out_11, out_12, out_13, out_14, out_15, out_16, out_17, out_18, O0
endmodule

module _4_bit_adder (
  input  in_1,
  input  in_2,
  input  in_3,
  input  in_4,
  input  in_5,
  input  in_6,
  input  in_7,
  input  in_8,
  output out_9,
  output out_10,
  output out_11,
  output out_12,
  output out_13
);

  wire full_adder_3_2_carry, full_adder_3_3_carry, half_adder_1_carry;

  full_adder_3 full_adder_3_1 (.in_carry(full_adder_3_2_carry), .Rin(in_5), .Lin(in_1), .SUM(out_9), .CARRY(out_13));
  full_adder_3 full_adder_3_2 (
    .in_carry(full_adder_3_3_carry), .Rin(in_6), .Lin(in_2), .SUM(out_10), .CARRY(full_adder_3_2_carry));
  full_adder_3 full_adder_3_3 (
    .in_carry(half_adder_1_carry), .Rin(in_7), .Lin(in_3), .SUM(out_11), .CARRY(full_adder_3_3_carry));
  half_adder half_adder_1 (.Right(in_8), .Left(in_4), .SUM(out_12), .CARRY(half_adder_1_carry));

  // Notes on the sheet:
  //   Full-Adder 3
  //   Overflow bit
  //   Full-Adder 2
  //   Status output
  //   Left Register
  //   Full-Adder 1
  //   Half-Adder
  //   A output
  //   A Register
  //   Right Register
endmodule

module half_adder (
  input  Right,
  input  Left,
  output SUM,
  output CARRY
);

  xor xor_1 (SUM, Right, Left);
  and and_1 (CARRY, Right, Left);
endmodule

module full_adder_3 (
  input  in_carry,
  input  Rin,
  input  Lin,
  output SUM,
  output CARRY
);

  wire half_adder_1_carry, half_adder_1_sum, half_adder_2_carry;

  half_adder half_adder_1 (.Right(Rin), .Left(Lin), .SUM(half_adder_1_sum), .CARRY(half_adder_1_carry));
  half_adder half_adder_2 (.Right(in_carry), .Left(half_adder_1_sum), .SUM(SUM), .CARRY(half_adder_2_carry));
  or or_1 (CARRY, half_adder_2_carry, half_adder_1_carry);
endmodule

module Shift_1_3 (
  input  b7,
  input  in_2,
  input  in_3,
  input  in_4,
  input  in_5,
  input  in_6,
  input  in_7,
  input  b0,
  input  ZERO,
  output O8,
  output out_11,
  output out_12,
  output out_13,
  output out_14,
  output out_15,
  output out_16,
  output out_17,
  output O0
);

  wire and_1_out, and_2_out, or_1_out;

  and and_1 (and_1_out, b7, in_3);
  and and_2 (and_2_out, b7, in_2);
  or or_1 (or_1_out, and_1_out, and_2_out);
  _4_bit_adder u_4_bit_adder_1 (
    .in_1(ZERO), .in_2(or_1_out), .in_3(and_2_out), .in_4(and_1_out), .in_5(ZERO), .in_6(ZERO),
    .in_7(or_1_out), .in_8(or_1_out), .out_9(O8), .out_10(out_11), .out_11(out_12), .out_12(out_13));  // open: out_13

  assign O0 = b0;
  assign out_14 = in_4;
  assign out_15 = in_5;
  assign out_16 = in_6;
  assign out_17 = in_7;
endmodule

module shift_4 (
  input  b8,
  input  in_2,
  input  in_3,
  input  in_4,
  input  in_5,
  input  in_6,
  input  in_7,
  input  in_8,
  input  b0,
  input  ZERO,
  output out_11,
  output out_12,
  output out_13,
  output out_14,
  output out_15,
  output out_16,
  output out_17,
  output out_18,
  output O0,
  output O9
);

  wire and_1_out, or_1_out, or_2_out;

  _4_bit_adder u_4_bit_adder_1 (
    .in_1(in_2), .in_2(in_3), .in_3(in_4), .in_4(in_5), .in_5(ZERO), .in_6(ZERO), .in_7(or_2_out),
    .in_8(or_2_out), .out_13(out_11), .out_9(out_12), .out_10(out_13), .out_11(out_14), .out_12(out_15));
  or or_1 (or_1_out, in_4, in_5);
  and and_1 (and_1_out, in_3, or_1_out);
  or or_2 (or_2_out, in_2, and_1_out);

  assign O0 = b0;
  assign O9 = b8;
  assign out_16 = in_6;
  assign out_17 = in_7;
  assign out_18 = in_8;
endmodule
