// Logisim project The-i273-v10.1.0.circ as structural Verilog
module main (
  input  _9,
  input  _8,
  input  _7,
  input  _6,
  input  _5,
  input  _4,
  input  _3,
  input  _2,
  input  _1,
  input  _0,
  input  in_11,
  input  in_12
);

  wire alu_1_negative, alu_1_overflow, alu_1_zero, and_1_out, and_2_out, and_3_out, and_4_out, and_5_out,
       and_6_out, and_7_out, clock_1_out, Hundreds_down, Hundreds_left_up, Hundreds_leftdown, Hundreds_mid,
       Hundreds_right_down, Hundreds_right_up, Hundreds_up, Ones_down, Ones_left_up, Ones_leftdown, Ones_mid,
       Ones_right_down, Ones_right_up, Ones_up, or_1_p1, or_1_p2, TEH_BRAIN_input_r1, TEH_BRAIN_input_r2,
       TEH_BRAIN_output_r1, TEH_BRAIN_output_r2, Tens_down, Tens_left_up, Tens_leftdown, Tens_mid,
       Tens_right_down, Tens_right_up, Tens_up, undriven, undriven_2, undriven_4, undriven_6, undriven_7,
       undriven_8, undriven_9, undriven_10, undriven_11, undriven_12, undriven_13, undriven_14, undriven_15;
  wire [1:0] undriven_3;
  wire [2:0] STATUS_overflow_2;
  wire [3:0] adder_1_out, AR_output_nibble, Bin__to_BCD_h, Bin__to_BCD_o, Bin__to_BCD_t,
       inputtobinary_1_out_11, IR_output_byte, IR_output_byte_2, MAR_output_nibble, multiplexer_2_out,
       multiplexer_5_out, PC_output_nibble;
  wire [7:0] alu_1_byte_out, and_8_out, demultiplexer_1_out0, demultiplexer_1_out1, demultiplexer_1_out2,
       demultiplexer_4_out0, DR_output_byte, MBR_output_byte, multiplexer_1_out, multiplexer_3_out,
       multiplexer_4_out, multiplexer_7_out, R1_output_byte, R2_output_byte, ram_1__0_2, undriven_5;

  Clock clock_1 (.out(clock_1_out));
  _8_bit_Register IR (
    .Input_Byte(demultiplexer_1_out2), .Clock(clock_1_out), .Output_Byte({IR_output_byte, IR_output_byte_2}));
  Multiplexer #(.width(8)) multiplexer_1 (
    .in0(demultiplexer_1_out1), .in1(demultiplexer_1_out0), .out(multiplexer_1_out), .sel(undriven),
    .en(in_11));
  _8_bit_Register MBR (.Input_Byte(multiplexer_1_out), .Clock(and_1_out), .Output_Byte(MBR_output_byte));
  and and_1 (and_1_out, clock_1_out, in_11);
  CU TEH_BRAIN (
    .Clock(clock_1_out), .Op_Code(IR_output_byte), .Input_R1(TEH_BRAIN_input_r1),
    .Output_R1(TEH_BRAIN_output_r1), .input_R2(TEH_BRAIN_input_r2), .output_R2(TEH_BRAIN_output_r2));  // open: Mux, in_R, in_L, Subtract, input_Aout, output_Aout, Input_STATUS, MAR____PC, MAR____IR, DR____SYSTEM, DR____RAM, DR____SYSTEM_2, DR____RAM_2, MBR____CPU, MBR____System, MBR____IR, MBR____System_2, MBR____CPU_2, PRT_enabler, INP_enabler, PC____INC, PC____IR
  Demultiplexer #(.select(2), .width(8)) demultiplexer_1 (
    .out0(demultiplexer_1_out0), .out1(demultiplexer_1_out1), .out2(demultiplexer_1_out2),
    .in(MBR_output_byte), .sel(undriven_3), .en(undriven_2));  // open: out3
  and and_2 (and_2_out, clock_1_out, in_12);
  Multiplexer #(.width(4)) multiplexer_2 (
    .in0(IR_output_byte_2), .in1(PC_output_nibble), .out(multiplexer_2_out), .sel(undriven_4), .en(in_12));
  _4_bit_Register MAR (.Input_Nibble(multiplexer_2_out), .Clock(and_2_out), .Output_Nibble(MAR_output_nibble));
  Demultiplexer #(.width(8)) demultiplexer_2 (
    .out0(demultiplexer_1_out1), .in(R1_output_byte), .sel(1'b0), .en(TEH_BRAIN_output_r1));  // open: out1
  _8_bit_Register R1 (.Input_Byte(multiplexer_3_out), .Clock(and_3_out), .Output_Byte(R1_output_byte));
  and and_3 (and_3_out, clock_1_out, TEH_BRAIN_input_r1);
  Multiplexer #(.width(8)) multiplexer_3 (
    .in0(demultiplexer_1_out1), .out(multiplexer_3_out), .sel(1'b0), .en(TEH_BRAIN_input_r1));  // open: in1
  Demultiplexer #(.width(8)) demultiplexer_3 (
    .out0(demultiplexer_1_out1), .in(R2_output_byte), .sel(1'b0), .en(TEH_BRAIN_output_r2));  // open: out1
  _8_bit_Register R2 (.Input_Byte(multiplexer_4_out), .Clock(and_4_out), .Output_Byte(R2_output_byte));
  and and_4 (and_4_out, clock_1_out, TEH_BRAIN_input_r2);
  Multiplexer #(.width(8)) multiplexer_4 (
    .in0(demultiplexer_1_out1), .in1(undriven_5), .out(multiplexer_4_out), .sel(1'b0), .en(TEH_BRAIN_input_r2));
  and and_5 (and_5_out, clock_1_out, undriven_10);
  _4_bit_Register PC (.Input_Nibble(multiplexer_5_out), .Clock(and_5_out), .Output_Nibble(PC_output_nibble));
  Multiplexer #(.width(4)) multiplexer_5 (
    .in0(adder_1_out), .in1(IR_output_byte_2), .out(multiplexer_5_out), .sel(undriven_13), .en(undriven_10));
  Multiplexer #(.width(8)) multiplexer_6 (
    .in0(alu_1_byte_out), .out(demultiplexer_1_out1), .sel(1'b0), .en(undriven_12));  // open: in1
  ALU alu_1 (
    .INPUT(demultiplexer_1_out1), .Clock(clock_1_out), ._0_R__1_L(undriven_6), .Enable(undriven_7),
    .ANS_Enable(undriven_8), ._0_ADD__1_SUB(undriven_9), .Byte_Out(alu_1_byte_out),
    .Overflow(alu_1_overflow), .Negative(alu_1_negative), .Zero(alu_1_zero));
  and and_6 (and_6_out, undriven_11, clock_1_out);
  Adder #(.width(4)) adder_1 (.a(4'b0001), .b(PC_output_nibble), .out(adder_1_out));  // open: cin, cout
  STATUS_Register STATUS (
    .Overflow(alu_1_overflow), .Negative(alu_1_negative), .Zero(alu_1_zero), .Clock(and_6_out),
    .Overflow_2(STATUS_overflow_2[0]), .Negative_2(STATUS_overflow_2[1]), .Zero_2(STATUS_overflow_2[2]));
  // OR_Gate or_1: pin names not known; wires that end beside it: or_1_p1, or_1_p2
  _4_bit_Register AR (.Input_Nibble(MAR_output_nibble), .Clock(clock_1_out), .Output_Nibble(AR_output_nibble));
  Demultiplexer #(.width(8)) demultiplexer_4 (
    .out0(demultiplexer_4_out0), .out1(demultiplexer_1_out0), .in(DR_output_byte), .sel(or_1_p1), .en(or_1_p2));
  _8_bit_Register DR (.Input_Byte(multiplexer_7_out), .Clock(clock_1_out), .Output_Byte(DR_output_byte));
  and and_7 (and_7_out, clock_1_out, undriven_14);
  Multiplexer #(.width(8)) multiplexer_7 (
    .in0(demultiplexer_1_out0), .in1(ram_1__0_2), .out(multiplexer_7_out), .sel(or_1_p1), .en(and_7_out));
  ram ram_1 (
    .Add__Nibble(AR_output_nibble), .Clk(clock_1_out), .W_0__R_1(or_1_p1), ._0(demultiplexer_4_out0[0]),
    ._1(demultiplexer_4_out0[1]), ._2(demultiplexer_4_out0[2]), ._3(demultiplexer_4_out0[3]),
    ._4(demultiplexer_4_out0[4]), ._5(demultiplexer_4_out0[5]), ._6(demultiplexer_4_out0[6]),
    ._7(demultiplexer_4_out0[7]), ._0_2(ram_1__0_2[0]), ._1_2(ram_1__0_2[1]), ._2_2(ram_1__0_2[2]),
    ._3_2(ram_1__0_2[3]), ._4_2(ram_1__0_2[4]), ._5_2(ram_1__0_2[5]), ._6_2(ram_1__0_2[6]),
    ._7_2(ram_1__0_2[7]));
  assign and_8_out = {8{1'b1}} & demultiplexer_1_out0;  // AND_Gate and_8, 8 bits wide
  Binary_to_BCD Bin__to_BCD (.in_1(and_8_out), .H(Bin__to_BCD_h), .T(Bin__to_BCD_t), .O(Bin__to_BCD_o));
  Multiplexer #(.width(8)) multiplexer_8 (
    .in0({4'b0000, inputtobinary_1_out_11}), .out(demultiplexer_1_out0), .sel(1'b0), .en(undriven_15));  // open: in1
  BCDtoDigit Hundreds (
    .in_1(Bin__to_BCD_h), .right_up(Hundreds_right_up), .up(Hundreds_up), .left_up(Hundreds_left_up),
    .mid(Hundreds_mid), .leftdown(Hundreds_leftdown), .down(Hundreds_down), .right_down(Hundreds_right_down));
  _7_Segment_Display u_7_segment_display_1 (
    .g(Hundreds_mid), .f(Hundreds_left_up), .a(Hundreds_up), .b(Hundreds_right_up), .e(Hundreds_leftdown),
    .d(Hundreds_down), .c(Hundreds_right_down));  // open: dp
  InputtoBinary inputtobinary_1 (
    ._0(_0), ._1(_1), ._2(_2), ._3(_3), ._4(_4), ._5(_5), ._6(_6), ._7(_7), ._8(_8), ._9(_9),
    .out_11(inputtobinary_1_out_11));
  BCDtoDigit Tens (
    .in_1(Bin__to_BCD_t), .right_up(Tens_right_up), .up(Tens_up), .left_up(Tens_left_up), .mid(Tens_mid),
    .leftdown(Tens_leftdown), .down(Tens_down), .right_down(Tens_right_down));
  _7_Segment_Display u_7_segment_display_2 (
    .g(Tens_mid), .f(Tens_left_up), .a(Tens_up), .b(Tens_right_up), .e(Tens_leftdown), .d(Tens_down),
    .c(Tens_right_down));  // open: dp
  BCDtoDigit Ones (
    .in_1(Bin__to_BCD_o), .right_up(Ones_right_up), .up(Ones_up), .left_up(Ones_left_up), .mid(Ones_mid),
    .leftdown(Ones_leftdown), .down(Ones_down), .right_down(Ones_right_down));
  _7_Segment_Display u_7_segment_display_3 (
    .g(Ones_mid), .f(Ones_left_up), .a(Ones_up), .b(Ones_right_up), .e(Ones_leftdown), .d(Ones_down),
    .c(Ones_right_down));  // open: dp

  // Notes on the sheet:
  //   Clock
  //   R2-R and R1-R are used to select which of both are in the left register => we can use exact same pattern of operations for ADD ADD SUB SUB
  //   Incrementer
endmodule

module CU (
  input  [1:0] Mux,
  input  Clock,
  input  [3:0] Op_Code,
  output Input_R1,
  output Output_R1,
  output input_R2,
  output output_R2,
  output in_R,
  output in_L,
  output Subtract,
  output input_Aout,
  output output_Aout,
  output Input_STATUS,
  output MAR____PC,
  output MAR____IR,
  output DR____SYSTEM,
  output DR____RAM,
  output DR____SYSTEM_2,
  output DR____RAM_2,
  output MBR____CPU,
  output MBR____System,
  output MBR____IR,
  output MBR____System_2,
  output MBR____CPU_2,
  output PRT_enabler,
  output INP_enabler,
  output PC____INC,
  output PC____IR
);

  wire and_1_out, and_2_out, and_3_out, and_4_out, and_5_out, and_6_out, and_7_out, and_8_out, and_9_out,
       and_10_out, and_11_out, and_12_out, and_13_out, and_14_out, and_15_out, and_16_out, decoder_1_out0,
       decoder_1_out2, decoder_1_out3, decoder_1_out4, decoder_1_out5, decoder_1_out6, decoder_1_out7,
       decoder_1_out8, decoder_1_out9, decoder_1_out10, decoder_1_out11, decoder_1_out12, decoder_1_out13,
       decoder_1_out14, decoder_1_out15, decoder_2_out8, decoder_2_out9, decoder_2_out10, decoder_2_out11,
       decoder_2_out12, decoder_2_out13, decoder_2_out16, decoder_2_out17, decoder_2_out18, decoder_2_out19,
       decoder_2_out22, decoder_2_out23, decoder_2_out24, decoder_2_out25, decoder_3_out1, decoder_3_out2,
       decoder_3_out3, decoder_3_out4, decoder_3_out8, decoder_3_out9, decoder_3_out10, decoder_3_out20,
       decoder_3_out21, decoder_3_out22, decoder_3_out24, decoder_3_out25, decoder_3_out26, or_1_out,
       or_2_out, or_3_out, or_4_out, or_5_out, or_6_out, or_7_out, or_8_out, or_14_out;
  wire [4:0] adder_1_out, d_ff_5_q, multiplexer_1_out, or_9_out;

  Adder #(.width(5)) adder_1 (.a(5'b00001), .b(d_ff_5_q), .out(adder_1_out));  // open: cin, cout
  Decoder #(.select(4), .enable("false")) decoder_1 (
    .out0(decoder_1_out0), .out2(decoder_1_out2), .out3(decoder_1_out3), .out4(decoder_1_out4),
    .out5(decoder_1_out5), .out6(decoder_1_out6), .out7(decoder_1_out7), .out8(decoder_1_out8),
    .out9(decoder_1_out9), .out10(decoder_1_out10), .out11(decoder_1_out11), .out12(decoder_1_out12),
    .out13(decoder_1_out13), .out14(decoder_1_out14), .out15(decoder_1_out15), .sel(Op_Code));  // open: out1
  or or_1 (or_1_out, decoder_1_out2, decoder_1_out3);
  or or_2 (or_2_out, decoder_1_out4, decoder_1_out5);
  or or_3 (or_3_out, decoder_1_out8, decoder_1_out9);
  or or_4 (or_4_out, decoder_1_out6, decoder_1_out7);
  or or_5 (or_5_out, decoder_1_out10, decoder_1_out11);
  or or_6 (or_6_out, decoder_1_out12, decoder_1_out13);
  or or_7 (or_7_out, decoder_1_out14, decoder_1_out15);
  D_Flip_Flop d_ff_1 (.clk(Clock), .D(multiplexer_1_out[4]), .Q(d_ff_5_q[4]));  // open: Qn, preset, en, reset
  Multiplexer #(.select(2), .width(5), .enable("false")) multiplexer_1 (
    .in0(adder_1_out), .in1(or_9_out), .out(multiplexer_1_out), .sel(Mux));  // open: in2, in3
  or or_8 (or_8_out, or_1_out, or_2_out, or_3_out);
  D_Flip_Flop d_ff_2 (.clk(Clock), .D(multiplexer_1_out[3]), .Q(d_ff_5_q[3]));  // open: Qn, preset, en, reset
  buf or_9 (or_9_out[0], or_6_out);  // OR_Gate
  buf or_10 (or_9_out[1], or_3_out);  // OR_Gate
  or or_11 (or_9_out[2], or_3_out, or_5_out);
  or or_12 (or_9_out[3], or_1_out, or_4_out, or_7_out);
  or or_13 (or_9_out[4], or_2_out, or_3_out, or_5_out, or_7_out);
  or or_14 (or_14_out, or_4_out, or_5_out, or_6_out, or_7_out);
  D_Flip_Flop d_ff_3 (.clk(Clock), .D(multiplexer_1_out[2]), .Q(d_ff_5_q[2]));  // open: Qn, preset, en, reset
  D_Flip_Flop d_ff_4 (.clk(Clock), .D(multiplexer_1_out[1]), .Q(d_ff_5_q[1]));  // open: Qn, preset, en, reset
  D_Flip_Flop d_ff_5 (.clk(Clock), .D(multiplexer_1_out[0]), .Q(d_ff_5_q[0]));  // open: Qn, preset, en, reset
  Decoder #(.select(5)) decoder_2 (
    .out8(decoder_2_out8), .out9(decoder_2_out9), .out10(decoder_2_out10), .out11(decoder_2_out11),
    .out12(decoder_2_out12), .out13(decoder_2_out13), .out16(decoder_2_out16), .out17(decoder_2_out17),
    .out18(decoder_2_out18), .out19(decoder_2_out19), .out22(decoder_2_out22), .out23(decoder_2_out23),
    .out24(decoder_2_out24), .out25(decoder_2_out25), .sel(d_ff_5_q), .en(or_8_out));  // open: out0, out1, out2, out3, out4, out5, out6, out7, out14, out15, out20, out21, out26, out27, out28, out29, out30, out31
  Decoder #(.select(5)) decoder_3 (
    .out1(decoder_3_out1), .out2(decoder_3_out2), .out3(decoder_3_out3), .out4(decoder_3_out4),
    .out8(decoder_3_out8), .out9(decoder_3_out9), .out10(decoder_3_out10), .out20(decoder_3_out20),
    .out21(decoder_3_out21), .out22(decoder_3_out22), .out24(decoder_3_out24), .out25(decoder_3_out25),
    .out26(decoder_3_out26), .sel(d_ff_5_q), .en(or_14_out));  // open: out0, out5, out6, out7, out11, out12, out13, out14, out15, out16, out17, out18, out19, out23, out27, out28, out29, out30, out31
  and and_1 (and_1_out, decoder_2_out12, ~Op_Code[0]);  // AND_Gate
  and and_2 (and_2_out, decoder_3_out3, ~Op_Code[0]);  // AND_Gate
  and and_3 (and_3_out, decoder_2_out24, ~Op_Code[0]);  // AND_Gate
  and and_4 (and_4_out, decoder_3_out25, ~Op_Code[0]);  // AND_Gate
  and and_5 (and_5_out, decoder_2_out16, ~Op_Code[0]);  // AND_Gate
  and and_6 (and_6_out, decoder_3_out20, ~Op_Code[0]);  // AND_Gate
  and and_7 (and_7_out, decoder_2_out12, Op_Code[0]);
  and and_8 (and_8_out, decoder_3_out3, Op_Code[0]);
  and and_9 (and_9_out, decoder_2_out24, Op_Code[0]);
  and and_10 (and_10_out, decoder_3_out25, Op_Code[0]);
  and and_11 (and_11_out, decoder_2_out16, Op_Code[0]);
  and and_12 (and_12_out, decoder_3_out20, Op_Code[0]);
  and and_13 (and_13_out, decoder_3_out1, ~Op_Code[0]);  // AND_Gate
  and and_14 (and_14_out, decoder_3_out2, Op_Code[0]);
  and and_15 (and_15_out, Op_Code[0], decoder_3_out1);
  and and_16 (and_16_out, decoder_3_out2, ~Op_Code[0]);  // AND_Gate
  or or_15 (Input_R1, and_1_out, and_2_out, and_3_out, and_4_out);
  or or_16 (Output_R1, and_5_out, decoder_2_out22, decoder_3_out1, decoder_3_out8, and_6_out);
  or or_17 (input_R2, and_7_out, and_8_out, and_9_out, and_10_out);
  or or_18 (output_R2, and_11_out, decoder_2_out23, decoder_3_out2, decoder_3_out9, and_12_out);
  or or_19 (in_R, decoder_2_out22, and_13_out, and_14_out, decoder_3_out8);
  or or_20 (in_L, decoder_2_out23, and_15_out, and_16_out, decoder_3_out9);
  or or_21 (Subtract, decoder_3_out2, decoder_3_out9);
  or or_22 (input_Aout, decoder_2_out23, decoder_3_out2, decoder_3_out9);
  or or_23 (output_Aout, decoder_2_out24, decoder_3_out3);
  or or_24 (Input_STATUS, decoder_2_out23, decoder_3_out2, decoder_3_out9);
  // OR_Gate or_25 has open pins: out=MAR____PC
  or or_26 (MAR____IR, decoder_2_out8, decoder_2_out16);
  buf or_27 (DR____SYSTEM, decoder_2_out17);  // OR_Gate
  buf or_28 (DR____RAM, decoder_2_out10);  // OR_Gate
  buf or_29 (DR____SYSTEM_2, decoder_2_out11);  // OR_Gate
  buf or_30 (DR____RAM_2, decoder_2_out18);  // OR_Gate
  or or_31 (MBR____CPU, decoder_2_out16, decoder_3_out20);
  or or_32 (MBR____System, decoder_2_out11, decoder_3_out24);
  // OR_Gate or_33 has open pins: out=MBR____IR
  or or_34 (MBR____System_2, decoder_2_out17, decoder_3_out21);
  or or_35 (MBR____CPU_2, decoder_2_out12, decoder_3_out25);
  buf or_36 (PRT_enabler, decoder_3_out21);  // OR_Gate
  buf or_37 (INP_enabler, decoder_3_out24);  // OR_Gate
  // OR_Gate or_38 has open pins: out=PC____INC
  // OR_Gate or_39 has open pins: out=PC____IR
  // AND_Gate and_17 is placed but not wired

  // Notes on the sheet:
  //   Increment
  //   STP
  //   LD
  //   STR
  //   ADD
  //   PRT
  //   SUB
  //   INP
  //   To beq or not to beq
  //   MSB
  //   0 = Increment
  //   1 = Fetch (from op-code)
  //   2 = Fetch address (00001) const.
  //   LSB
  //   MSB
  //   LSB
  //   LD
  //   STR
  //   ADD
  //   SUB
  //   PRT
  //   INP
  //   BEQ / BNQ
  //   Check zero and pseudofetch
  //   This is MAR to AR, just make sure signal is left alone
  //   FETCH
  //   FETCH
  //   FETCH
  //   FETCH
  //   FETCH
  //   FETCH
endmodule

// RAM
module ram (
  input  [3:0] Add__Nibble,
  input  Clk,
  input  W_0__R_1,
  input  _0,
  input  _1,
  input  _2,
  input  _3,
  input  _4,
  input  _5,
  input  _6,
  input  _7,
  output _0_2,
  output _1_2,
  output _2_2,
  output _3_2,
  output _4_2,
  output _5_2,
  output _6_2,
  output _7_2
);

  wire and_1_out, and_2_out, and_3_out, and_4_out, and_5_out, and_6_out, and_7_out, and_8_out, and_9_out,
       and_10_out, and_11_out, and_12_out, and_13_out, and_14_out, and_15_out, and_16_out, and_17_out,
       and_18_out, and_19_out, and_20_out, and_21_out, and_22_out, and_23_out, and_24_out, and_25_out,
       and_26_out, and_27_out, and_28_out, and_29_out, and_30_out, and_31_out, and_32_out, and_33_out,
       and_34_out, and_35_out, and_36_out, and_37_out, and_38_out, and_39_out, and_40_out, and_41_out,
       and_42_out, and_43_out, and_44_out, and_45_out, and_46_out, and_47_out, and_48_out, and_49_out,
       and_50_out, and_51_out, and_52_out, and_53_out, and_54_out, and_55_out, and_56_out, and_57_out,
       and_58_out, and_59_out, and_60_out, and_61_out, and_62_out, and_63_out, and_64_out, and_65_out,
       and_66_out, and_67_out, and_68_out, and_69_out, and_70_out, and_71_out, and_72_out, and_73_out,
       and_74_out, and_75_out, and_76_out, and_77_out, and_78_out, and_79_out, and_80_out, and_81_out,
       and_82_out, and_83_out, and_84_out, and_85_out, and_86_out, and_87_out, and_88_out, and_89_out,
       and_90_out, and_91_out, and_92_out, and_93_out, and_94_out, and_95_out, and_96_out, and_97_out,
       and_98_out, and_99_out, and_100_out, and_101_out, and_102_out, and_103_out, and_104_out, and_105_out,
       and_106_out, and_107_out, and_108_out, and_109_out, and_110_out, and_111_out, and_112_out,
       and_113_out, and_114_out, and_115_out, and_116_out, and_117_out, and_118_out, and_119_out,
       and_120_out, and_121_out, and_122_out, and_123_out, and_124_out, and_125_out, and_126_out,
       and_127_out, and_128_out, and_129_out, and_130_out, and_131_out, and_132_out, and_133_out,
       and_134_out, and_135_out, and_136_out, and_137_out, and_138_out, and_139_out, and_140_out,
       and_141_out, and_142_out, and_143_out, and_144_out, d_ff_1_q, d_ff_2_q, d_ff_3_q, d_ff_4_q, d_ff_5_q,
       d_ff_6_q, d_ff_7_q, d_ff_8_q, d_ff_9_q, d_ff_10_q, d_ff_11_q, d_ff_12_q, d_ff_13_q, d_ff_14_q,
       d_ff_15_q, d_ff_16_q, d_ff_17_q, d_ff_18_q, d_ff_19_q, d_ff_20_q, d_ff_21_q, d_ff_22_q, d_ff_23_q,
       d_ff_24_q, d_ff_25_q, d_ff_26_q, d_ff_27_q, d_ff_28_q, d_ff_29_q, d_ff_30_q, d_ff_31_q, d_ff_32_q,
       d_ff_33_q, d_ff_34_q, d_ff_35_q, d_ff_36_q, d_ff_37_q, d_ff_38_q, d_ff_39_q, d_ff_40_q, d_ff_41_q,
       d_ff_42_q, d_ff_43_q, d_ff_44_q, d_ff_45_q, d_ff_46_q, d_ff_47_q, d_ff_48_q, d_ff_49_q, d_ff_50_q,
       d_ff_51_q, d_ff_52_q, d_ff_53_q, d_ff_54_q, d_ff_55_q, d_ff_56_q, d_ff_57_q, d_ff_58_q, d_ff_59_q,
       d_ff_60_q, d_ff_61_q, d_ff_62_q, d_ff_63_q, d_ff_64_q, d_ff_65_q, d_ff_66_q, d_ff_67_q, d_ff_68_q,
       d_ff_69_q, d_ff_70_q, d_ff_71_q, d_ff_72_q, d_ff_73_q, d_ff_74_q, d_ff_75_q, d_ff_76_q, d_ff_77_q,
       d_ff_78_q, d_ff_79_q, d_ff_80_q, d_ff_81_q, d_ff_82_q, d_ff_83_q, d_ff_84_q, d_ff_85_q, d_ff_86_q,
       d_ff_87_q, d_ff_88_q, d_ff_89_q, d_ff_90_q, d_ff_91_q, d_ff_92_q, d_ff_93_q, d_ff_94_q, d_ff_95_q,
       d_ff_96_q, d_ff_97_q, d_ff_98_q, d_ff_99_q, d_ff_100_q, d_ff_101_q, d_ff_102_q, d_ff_103_q,
       d_ff_104_q, d_ff_105_q, d_ff_106_q, d_ff_107_q, d_ff_108_q, d_ff_109_q, d_ff_110_q, d_ff_111_q,
       d_ff_112_q, d_ff_113_q, d_ff_114_q, d_ff_115_q, d_ff_116_q, d_ff_117_q, d_ff_118_q, d_ff_119_q,
       d_ff_120_q, d_ff_121_q, d_ff_122_q, d_ff_123_q, d_ff_124_q, d_ff_125_q, d_ff_126_q, d_ff_127_q,
       d_ff_128_q, decoder_1_out0, decoder_1_out1, decoder_1_out2, decoder_1_out3, decoder_1_out4,
       decoder_1_out5, decoder_1_out6, decoder_1_out7, decoder_1_out8, decoder_1_out9, decoder_1_out10,
       decoder_1_out11, decoder_1_out12, decoder_1_out13, decoder_1_out14, decoder_1_out15, not_1_out;
  wire [7:0] and_145_out, and_153_out, and_161_out, and_169_out, and_177_out, and_185_out, and_193_out,
       and_201_out, and_209_out, and_217_out, and_225_out, and_233_out, and_241_out, and_249_out,
       and_257_out, and_265_out;

  Decoder #(.select(4), .enable("false")) decoder_1 (
    .out0(decoder_1_out0), .out1(decoder_1_out1), .out2(decoder_1_out2), .out3(decoder_1_out3),
    .out4(decoder_1_out4), .out5(decoder_1_out5), .out6(decoder_1_out6), .out7(decoder_1_out7),
    .out8(decoder_1_out8), .out9(decoder_1_out9), .out10(decoder_1_out10), .out11(decoder_1_out11),
    .out12(decoder_1_out12), .out13(decoder_1_out13), .out14(decoder_1_out14), .out15(decoder_1_out15),
    .sel(Add__Nibble));
  not not_1 (not_1_out, W_0__R_1);
  and and_1 (and_1_out, not_1_out, decoder_1_out0, Clk);
  and and_2 (and_2_out, not_1_out, decoder_1_out1, Clk);
  and and_3 (and_3_out, not_1_out, decoder_1_out2, Clk);
  and and_4 (and_4_out, not_1_out, not_1_out, decoder_1_out3, Clk);
  and and_5 (and_5_out, not_1_out, decoder_1_out4, Clk);
  and and_6 (and_6_out, not_1_out, decoder_1_out5, Clk);
  and and_7 (and_7_out, not_1_out, decoder_1_out6, Clk);
  and and_8 (and_8_out, not_1_out, decoder_1_out7, Clk);
  and and_9 (and_9_out, Clk, not_1_out, decoder_1_out9);
  and and_10 (and_10_out, Clk, decoder_1_out10, not_1_out);
  and and_11 (and_11_out, Clk, decoder_1_out11, not_1_out);
  and and_12 (and_12_out, Clk, decoder_1_out12, not_1_out);
  and and_13 (and_13_out, Clk, decoder_1_out13, not_1_out);
  and and_14 (and_14_out, Clk, not_1_out, decoder_1_out14);
  and and_15 (and_15_out, not_1_out, decoder_1_out15, Clk);
  and and_16 (and_16_out, _0, not_1_out, decoder_1_out0);
  and and_17 (and_17_out, _1, not_1_out, decoder_1_out0);
  and and_18 (and_18_out, _2, not_1_out, decoder_1_out0);
  and and_19 (and_19_out, _3, not_1_out, decoder_1_out0);
  and and_20 (and_20_out, not_1_out, decoder_1_out0, _4);
  and and_21 (and_21_out, not_1_out, decoder_1_out0, _5);
  and and_22 (and_22_out, not_1_out, decoder_1_out0, _6);
  and and_23 (and_23_out, _7, not_1_out, decoder_1_out0);
  and and_24 (and_24_out, decoder_1_out1, not_1_out, _0);
  and and_25 (and_25_out, _1, decoder_1_out1, not_1_out);
  and and_26 (and_26_out, decoder_1_out1, not_1_out, _2);
  and and_27 (and_27_out, decoder_1_out1, not_1_out, _3);
  and and_28 (and_28_out, not_1_out, decoder_1_out1, _4);
  and and_29 (and_29_out, _5, not_1_out, decoder_1_out1);
  and and_30 (and_30_out, _6, not_1_out, decoder_1_out1);
  and and_31 (and_31_out, _7, not_1_out, decoder_1_out1);
  and and_32 (and_32_out, _0, decoder_1_out2, not_1_out);
  and and_33 (and_33_out, _1, decoder_1_out2, not_1_out);
  and and_34 (and_34_out, _2, not_1_out, decoder_1_out2);
  and and_35 (and_35_out, _3, not_1_out, decoder_1_out2);
  and and_36 (and_36_out, _4, not_1_out, decoder_1_out2);
  and and_37 (and_37_out, _5, not_1_out, decoder_1_out2);
  and and_38 (and_38_out, _6, not_1_out, decoder_1_out2);
  and and_39 (and_39_out, _7, not_1_out, decoder_1_out2);
  and and_40 (and_40_out, not_1_out, decoder_1_out3, _0);
  and and_41 (and_41_out, _1, not_1_out, decoder_1_out3);
  and and_42 (and_42_out, _2, not_1_out, decoder_1_out3);
  and and_43 (and_43_out, _3, not_1_out, decoder_1_out3);
  and and_44 (and_44_out, _4, not_1_out, decoder_1_out3);
  and and_45 (and_45_out, _5, not_1_out, decoder_1_out3);
  and and_46 (and_46_out, _6, not_1_out, decoder_1_out3);
  and and_47 (and_47_out, _7, not_1_out, decoder_1_out3);
  and and_48 (and_48_out, decoder_1_out4, not_1_out, _0);
  and and_49 (and_49_out, _1, decoder_1_out4, not_1_out);
  and and_50 (and_50_out, _2, decoder_1_out4, not_1_out);
  and and_51 (and_51_out, _3, decoder_1_out4, not_1_out);
  and and_52 (and_52_out, _4, not_1_out, decoder_1_out4);
  and and_53 (and_53_out, _5, not_1_out, decoder_1_out4);
  and and_54 (and_54_out, _6, not_1_out, decoder_1_out4);
  and and_55 (and_55_out, _7, not_1_out, decoder_1_out4);
  and and_56 (and_56_out, not_1_out, decoder_1_out5, _0);
  and and_57 (and_57_out, _1, not_1_out, decoder_1_out5);
  and and_58 (and_58_out, _2, not_1_out, decoder_1_out5);
  and and_59 (and_59_out, _3, not_1_out, decoder_1_out5);
  and and_60 (and_60_out, _4, not_1_out, decoder_1_out5);
  and and_61 (and_61_out, not_1_out, decoder_1_out5, _5);
  and and_62 (and_62_out, _6, not_1_out, decoder_1_out5);
  and and_63 (and_63_out, decoder_1_out5, _7, not_1_out, decoder_1_out5);
  and and_64 (and_64_out, decoder_1_out6, decoder_1_out6, _0);
  and and_65 (and_65_out, _1, decoder_1_out6, not_1_out);
  and and_66 (and_66_out, not_1_out, decoder_1_out6, _2);
  and and_67 (and_67_out, _3, not_1_out, decoder_1_out6);
  and and_68 (and_68_out, _4, not_1_out, decoder_1_out6);
  and and_69 (and_69_out, _5, decoder_1_out6, not_1_out);
  and and_70 (and_70_out, _6, not_1_out, decoder_1_out6);
  and and_71 (and_71_out, _7, not_1_out, decoder_1_out6);
  and and_72 (and_72_out, decoder_1_out7, not_1_out, _0);
  and and_73 (and_73_out, decoder_1_out7, not_1_out, _1);
  and and_74 (and_74_out, decoder_1_out7, not_1_out, _2);
  and and_75 (and_75_out, not_1_out, decoder_1_out7, _3);
  and and_76 (and_76_out, not_1_out, decoder_1_out7, _4);
  and and_77 (and_77_out, _5, not_1_out, decoder_1_out7);
  and and_78 (and_78_out, _6, not_1_out, decoder_1_out7);
  and and_79 (and_79_out, not_1_out, _7, decoder_1_out7);
  and and_80 (and_80_out, Clk, decoder_1_out8, not_1_out);
  and and_81 (and_81_out, decoder_1_out8, not_1_out, not_1_out, _0);
  and and_82 (and_82_out, decoder_1_out8, not_1_out, _1);
  and and_83 (and_83_out, decoder_1_out8, not_1_out, _2);
  and and_84 (and_84_out, decoder_1_out8, not_1_out, _3);
  and and_85 (and_85_out, decoder_1_out8, not_1_out, _4);
  and and_86 (and_86_out, decoder_1_out8, not_1_out, _5);
  and and_87 (and_87_out, decoder_1_out8, not_1_out, _6);
  and and_88 (and_88_out, decoder_1_out8, not_1_out, _7);
  and and_89 (and_89_out, decoder_1_out9, not_1_out, _0);
  and and_90 (and_90_out, _1, not_1_out, decoder_1_out9);
  and and_91 (and_91_out, _2, not_1_out, decoder_1_out9);
  and and_92 (and_92_out, _3, not_1_out, decoder_1_out9);
  and and_93 (and_93_out, _4, not_1_out, decoder_1_out9);
  and and_94 (and_94_out, _5, decoder_1_out9, not_1_out);
  and and_95 (and_95_out, _6, decoder_1_out9, not_1_out);
  and and_96 (and_96_out, _7, decoder_1_out9, not_1_out);
  and and_97 (and_97_out, decoder_1_out10, not_1_out, _0);
  and and_98 (and_98_out, decoder_1_out10, not_1_out, _1);
  and and_99 (and_99_out, decoder_1_out10, not_1_out, _2);
  and and_100 (and_100_out, _3, decoder_1_out10, not_1_out);
  and and_101 (and_101_out, decoder_1_out10, not_1_out, _4);
  and and_102 (and_102_out, decoder_1_out10, not_1_out, _5);
  and and_103 (and_103_out, decoder_1_out10, not_1_out, _6);
  and and_104 (and_104_out, decoder_1_out10, not_1_out, _7);
  and and_105 (and_105_out, _0, decoder_1_out11, not_1_out);
  and and_106 (and_106_out, _1, not_1_out, decoder_1_out11);
  and and_107 (and_107_out, _2, not_1_out, decoder_1_out11);
  and and_108 (and_108_out, _3, not_1_out, decoder_1_out11);
  and and_109 (and_109_out, _4, not_1_out, decoder_1_out11);
  and and_110 (and_110_out, not_1_out, decoder_1_out11, _5);
  and and_111 (and_111_out, _6, not_1_out, decoder_1_out11);
  and and_112 (and_112_out, _7, not_1_out, decoder_1_out11);
  and and_113 (and_113_out, not_1_out, decoder_1_out12, _0);
  and and_114 (and_114_out, _1, not_1_out, decoder_1_out12);
  and and_115 (and_115_out, not_1_out, decoder_1_out12, _2);
  and and_116 (and_116_out, not_1_out, decoder_1_out12, _3);
  and and_117 (and_117_out, not_1_out, decoder_1_out12, _4);
  and and_118 (and_118_out, _5, not_1_out, decoder_1_out12);
  and and_119 (and_119_out, not_1_out, decoder_1_out12, _6);
  and and_120 (and_120_out, not_1_out, decoder_1_out12, _7);
  and and_121 (and_121_out, _0, not_1_out, decoder_1_out13);
  and and_122 (and_122_out, _1, not_1_out, decoder_1_out13);
  and and_123 (and_123_out, _2, not_1_out, decoder_1_out13);
  and and_124 (and_124_out, _3, not_1_out, decoder_1_out13);
  and and_125 (and_125_out, _4, not_1_out, decoder_1_out13);
  and and_126 (and_126_out, _5, not_1_out, decoder_1_out13);
  and and_127 (and_127_out, _6, not_1_out, decoder_1_out13);
  and and_128 (and_128_out, _7, not_1_out, decoder_1_out13);
  and and_129 (and_129_out, _0, decoder_1_out14, not_1_out);
  and and_130 (and_130_out, not_1_out, decoder_1_out14, _1);
  and and_131 (and_131_out, decoder_1_out14, _2, not_1_out);
  and and_132 (and_132_out, decoder_1_out14, not_1_out, _3);
  and and_133 (and_133_out, not_1_out, decoder_1_out14, _4);
  and and_134 (and_134_out, not_1_out, decoder_1_out14, _5);
  and and_135 (and_135_out, _6, not_1_out, decoder_1_out14);
  and and_136 (and_136_out, _7, decoder_1_out14, not_1_out);
  and and_137 (and_137_out, not_1_out, decoder_1_out15, _0);
  and and_138 (and_138_out, not_1_out, decoder_1_out15, _1);
  and and_139 (and_139_out, not_1_out, _2, decoder_1_out15);
  and and_140 (and_140_out, not_1_out, _3, decoder_1_out15);
  and and_141 (and_141_out, _4, not_1_out, decoder_1_out15);
  and and_142 (and_142_out, decoder_1_out15, _5, not_1_out);
  and and_143 (and_143_out, _6, decoder_1_out15, not_1_out);
  and and_144 (and_144_out, not_1_out, _7, decoder_1_out15);
  D_Flip_Flop d_ff_1 (.clk(and_1_out), .D(and_16_out), .Q(d_ff_1_q));  // open: Qn, preset, en, reset
  D_Flip_Flop d_ff_2 (.clk(and_1_out), .D(and_17_out), .Q(d_ff_2_q));  // open: Qn, preset, en, reset
  D_Flip_Flop d_ff_3 (.clk(and_1_out), .D(and_18_out), .Q(d_ff_3_q));  // open: Qn, preset, en, reset
  D_Flip_Flop d_ff_4 (.clk(and_1_out), .D(and_19_out), .Q(d_ff_4_q));  // open: Qn, preset, en, reset
  D_Flip_Flop d_ff_5 (.clk(and_1_out), .D(and_20_out), .Q(d_ff_5_q));  // open: Qn, preset, en, reset
  D_Flip_Flop d_ff_6 (.clk(and_1_out), .D(and_21_out), .Q(d_ff_6_q));  // open: Qn, preset, en, reset
  D_Flip_Flop d_ff_7 (.clk(and_1_out), .D(and_22_out), .Q(d_ff_7_q));  // open: Qn, preset, en, reset
  D_Flip_Flop d_ff_8 (.clk(and_1_out), .D(and_23_out), .Q(d_ff_8_q));  // open: Qn, preset, en, reset
  D_Flip_Flop d_ff_9 (.clk(and_2_out), .D(and_24_out), .Q(d_ff_9_q));  // open: Qn, preset, en, reset
  D_Flip_Flop d_ff_10 (.clk(and_2_out), .D(and_25_out), .Q(d_ff_10_q));  // open: Qn, preset, en, reset
  D_Flip_Flop d_ff_11 (.clk(and_2_out), .D(and_26_out), .Q(d_ff_11_q));  // open: Qn, preset, en, reset
  D_Flip_Flop d_ff_12 (.clk(and_2_out), .D(and_27_out), .Q(d_ff_12_q));  // open: Qn, preset, en, reset
  D_Flip_Flop d_ff_13 (.clk(and_2_out), .D(and_28_out), .Q(d_ff_13_q));  // open: Qn, preset, en, reset
  D_Flip_Flop d_ff_14 (.clk(and_2_out), .D(and_29_out), .Q(d_ff_14_q));  // open: Qn, preset, en, reset
  D_Flip_Flop d_ff_15 (.clk(and_2_out), .D(and_30_out), .Q(d_ff_15_q));  // open: Qn, preset, en, reset
  D_Flip_Flop d_ff_16 (.clk(and_2_out), .D(and_31_out), .Q(d_ff_16_q));  // open: Qn, preset, en, reset
  D_Flip_Flop d_ff_17 (.clk(and_3_out), .D(and_32_out), .Q(d_ff_17_q));  // open: Qn, preset, en, reset
  D_Flip_Flop d_ff_18 (.clk(and_3_out), .D(and_33_out), .Q(d_ff_18_q));  // open: Qn, preset, en, reset
  D_Flip_Flop d_ff_19 (.clk(and_3_out), .D(and_34_out), .Q(d_ff_19_q));  // open: Qn, preset, en, reset
  D_Flip_Flop d_ff_20 (.clk(and_3_out), .D(and_35_out), .Q(d_ff_20_q));  // open: Qn, preset, en, reset
  D_Flip_Flop d_ff_21 (.clk(and_3_out), .D(and_36_out), .Q(d_ff_21_q));  // open: Qn, preset, en, reset
  D_Flip_Flop d_ff_22 (.clk(and_3_out), .D(and_37_out), .Q(d_ff_22_q));  // open: Qn, preset, en, reset
  D_Flip_Flop d_ff_23 (.clk(and_3_out), .D(and_38_out), .Q(d_ff_23_q));  // open: Qn, preset, en, reset
  D_Flip_Flop d_ff_24 (.clk(and_3_out), .D(and_39_out), .Q(d_ff_24_q));  // open: Qn, preset, en, reset
  D_Flip_Flop d_ff_25 (.clk(and_4_out), .D(and_40_out), .Q(d_ff_25_q));  // open: Qn, preset, en, reset
  D_Flip_Flop d_ff_26 (.clk(and_4_out), .D(and_41_out), .Q(d_ff_26_q));  // open: Qn, preset, en, reset
  D_Flip_Flop d_ff_27 (.clk(and_4_out), .D(and_42_out), .Q(d_ff_27_q));  // open: Qn, preset, en, reset
  D_Flip_Flop d_ff_28 (.clk(and_4_out), .D(and_43_out), .Q(d_ff_28_q));  // open: Qn, preset, en, reset
  D_Flip_Flop d_ff_29 (.clk(and_4_out), .D(and_44_out), .Q(d_ff_29_q));  // open: Qn, preset, en, reset
  D_Flip_Flop d_ff_30 (.clk(and_4_out), .D(and_45_out), .Q(d_ff_30_q));  // open: Qn, preset, en, reset
  D_Flip_Flop d_ff_31 (.clk(and_4_out), .D(and_46_out), .Q(d_ff_31_q));  // open: Qn, preset, en, reset
  D_Flip_Flop d_ff_32 (.clk(and_4_out), .D(and_47_out), .Q(d_ff_32_q));  // open: Qn, preset, en, reset
  D_Flip_Flop d_ff_33 (.clk(and_5_out), .D(and_48_out), .Q(d_ff_33_q));  // open: Qn, preset, en, reset
  D_Flip_Flop d_ff_34 (.clk(and_5_out), .D(and_49_out), .Q(d_ff_34_q));  // open: Qn, preset, en, reset
  D_Flip_Flop d_ff_35 (.D(and_50_out), .Q(d_ff_35_q));  // open: clk, Qn, preset, en, reset
  D_Flip_Flop d_ff_36 (.clk(and_5_out), .D(and_51_out), .Q(d_ff_36_q));  // open: Qn, preset, en, reset
  D_Flip_Flop d_ff_37 (.clk(and_5_out), .D(and_52_out), .Q(d_ff_37_q));  // open: Qn, preset, en, reset
  D_Flip_Flop d_ff_38 (.clk(and_5_out), .D(and_53_out), .Q(d_ff_38_q));  // open: Qn, preset, en, reset
  D_Flip_Flop d_ff_39 (.clk(and_5_out), .D(and_54_out), .Q(d_ff_39_q));  // open: Qn, preset, en, reset
  D_Flip_Flop d_ff_40 (.clk(and_5_out), .D(and_55_out), .Q(d_ff_40_q));  // open: Qn, preset, en, reset
  D_Flip_Flop d_ff_41 (.clk(and_6_out), .D(and_56_out), .Q(d_ff_41_q));  // open: Qn, preset, en, reset
  D_Flip_Flop d_ff_42 (.clk(and_6_out), .D(and_57_out), .Q(d_ff_42_q));  // open: Qn, preset, en, reset
  D_Flip_Flop d_ff_43 (.clk(and_6_out), .D(and_58_out), .Q(d_ff_43_q));  // open: Qn, preset, en, reset
  D_Flip_Flop d_ff_44 (.clk(and_6_out), .D(and_59_out), .Q(d_ff_44_q));  // open: Qn, preset, en, reset
  D_Flip_Flop d_ff_45 (.clk(and_6_out), .D(and_60_out), .Q(d_ff_45_q));  // open: Qn, preset, en, reset
  D_Flip_Flop d_ff_46 (.clk(and_6_out), .D(and_61_out), .Q(d_ff_46_q));  // open: Qn, preset, en, reset
  D_Flip_Flop d_ff_47 (.clk(and_6_out), .D(and_62_out), .Q(d_ff_47_q));  // open: Qn, preset, en, reset
  D_Flip_Flop d_ff_48 (.clk(and_6_out), .D(and_63_out), .Q(d_ff_48_q));  // open: Qn, preset, en, reset
  D_Flip_Flop d_ff_49 (.clk(and_7_out), .D(and_64_out), .Q(d_ff_49_q));  // open: Qn, preset, en, reset
  D_Flip_Flop d_ff_50 (.clk(and_7_out), .D(and_65_out), .Q(d_ff_50_q));  // open: Qn, preset, en, reset
  D_Flip_Flop d_ff_51 (.clk(and_7_out), .D(and_66_out), .Q(d_ff_51_q));  // open: Qn, preset, en, reset
  D_Flip_Flop d_ff_52 (.D(and_67_out), .Q(d_ff_52_q));  // open: clk, Qn, preset, en, reset
  D_Flip_Flop d_ff_53 (.clk(and_7_out), .D(and_68_out), .Q(d_ff_53_q));  // open: Qn, preset, en, reset
  D_Flip_Flop d_ff_54 (.clk(and_7_out), .D(and_69_out), .Q(d_ff_54_q));  // open: Qn, preset, en, reset
  D_Flip_Flop d_ff_55 (.clk(and_7_out), .D(and_70_out), .Q(d_ff_55_q));  // open: Qn, preset, en, reset
  D_Flip_Flop d_ff_56 (.clk(and_7_out), .D(and_71_out), .Q(d_ff_56_q));  // open: Qn, preset, en, reset
  D_Flip_Flop d_ff_57 (.clk(and_8_out), .D(and_72_out), .Q(d_ff_57_q));  // open: Qn, preset, en, reset
  D_Flip_Flop d_ff_58 (.clk(and_8_out), .D(and_73_out), .Q(d_ff_58_q));  // open: Qn, preset, en, reset
  D_Flip_Flop d_ff_59 (.clk(and_8_out), .D(and_74_out), .Q(d_ff_59_q));  // open: Qn, preset, en, reset
  D_Flip_Flop d_ff_60 (.clk(and_8_out), .D(and_75_out), .Q(d_ff_60_q));  // open: Qn, preset, en, reset
  D_Flip_Flop d_ff_61 (.clk(and_8_out), .D(and_76_out), .Q(d_ff_61_q));  // open: Qn, preset, en, reset
  D_Flip_Flop d_ff_62 (.clk(and_8_out), .D(and_77_out), .Q(d_ff_62_q));  // open: Qn, preset, en, reset
  D_Flip_Flop d_ff_63 (.clk(and_8_out), .D(and_78_out), .Q(d_ff_63_q));  // open: Qn, preset, en, reset
  D_Flip_Flop d_ff_64 (.clk(and_8_out), .D(and_79_out), .Q(d_ff_64_q));  // open: Qn, preset, en, reset
  D_Flip_Flop d_ff_65 (.clk(and_80_out), .D(and_81_out), .Q(d_ff_65_q));  // open: Qn, preset, en, reset
  D_Flip_Flop d_ff_66 (.clk(and_80_out), .D(and_82_out), .Q(d_ff_66_q));  // open: Qn, preset, en, reset
  D_Flip_Flop d_ff_67 (.clk(and_80_out), .D(and_83_out), .Q(d_ff_67_q));  // open: Qn, preset, en, reset
  D_Flip_Flop d_ff_68 (.clk(and_80_out), .D(and_84_out), .Q(d_ff_68_q));  // open: Qn, preset, en, reset
  D_Flip_Flop d_ff_69 (.clk(and_80_out), .D(and_85_out), .Q(d_ff_69_q));  // open: Qn, preset, en, reset
  D_Flip_Flop d_ff_70 (.clk(and_80_out), .D(and_86_out), .Q(d_ff_70_q));  // open: Qn, preset, en, reset
  D_Flip_Flop d_ff_71 (.clk(and_80_out), .D(and_87_out), .Q(d_ff_71_q));  // open: Qn, preset, en, reset
  D_Flip_Flop d_ff_72 (.clk(and_80_out), .D(and_88_out), .Q(d_ff_72_q));  // open: Qn, preset, en, reset
  D_Flip_Flop d_ff_73 (.clk(and_9_out), .D(and_89_out), .Q(d_ff_73_q));  // open: Qn, preset, en, reset
  D_Flip_Flop d_ff_74 (.clk(and_9_out), .D(and_90_out), .Q(d_ff_74_q));  // open: Qn, preset, en, reset
  D_Flip_Flop d_ff_75 (.clk(and_9_out), .D(and_91_out), .Q(d_ff_75_q));  // open: Qn, preset, en, reset
  D_Flip_Flop d_ff_76 (.clk(and_9_out), .D(and_92_out), .Q(d_ff_76_q));  // open: Qn, preset, en, reset
  D_Flip_Flop d_ff_77 (.clk(and_9_out), .D(and_93_out), .Q(d_ff_77_q));  // open: Qn, preset, en, reset
  D_Flip_Flop d_ff_78 (.clk(and_9_out), .D(and_94_out), .Q(d_ff_78_q));  // open: Qn, preset, en, reset
  D_Flip_Flop d_ff_79 (.clk(and_9_out), .D(and_95_out), .Q(d_ff_79_q));  // open: Qn, preset, en, reset
  D_Flip_Flop d_ff_80 (.clk(and_9_out), .D(and_96_out), .Q(d_ff_80_q));  // open: Qn, preset, en, reset
  D_Flip_Flop d_ff_81 (.clk(and_10_out), .D(and_97_out), .Q(d_ff_81_q));  // open: Qn, preset, en, reset
  D_Flip_Flop d_ff_82 (.clk(and_10_out), .D(and_98_out), .Q(d_ff_82_q));  // open: Qn, preset, en, reset
  D_Flip_Flop d_ff_83 (.clk(and_10_out), .D(and_99_out), .Q(d_ff_83_q));  // open: Qn, preset, en, reset
  D_Flip_Flop d_ff_84 (.clk(and_10_out), .D(and_100_out), .Q(d_ff_84_q));  // open: Qn, preset, en, reset
  D_Flip_Flop d_ff_85 (.clk(and_10_out), .D(and_101_out), .Q(d_ff_85_q));  // open: Qn, preset, en, reset
  D_Flip_Flop d_ff_86 (.clk(and_10_out), .D(and_102_out), .Q(d_ff_86_q));  // open: Qn, preset, en, reset
  D_Flip_Flop d_ff_87 (.clk(and_10_out), .D(and_103_out), .Q(d_ff_87_q));  // open: Qn, preset, en, reset
  D_Flip_Flop d_ff_88 (.clk(and_10_out), .D(and_104_out), .Q(d_ff_88_q));  // open: Qn, preset, en, reset
  D_Flip_Flop d_ff_89 (.clk(and_11_out), .D(and_105_out), .Q(d_ff_89_q));  // open: Qn, preset, en, reset
  D_Flip_Flop d_ff_90 (.clk(and_11_out), .D(and_106_out), .Q(d_ff_90_q));  // open: Qn, preset, en, reset
  D_Flip_Flop d_ff_91 (.clk(and_11_out), .D(and_107_out), .Q(d_ff_91_q));  // open: Qn, preset, en, reset
  D_Flip_Flop d_ff_92 (.clk(and_11_out), .D(and_108_out), .Q(d_ff_92_q));  // open: Qn, preset, en, reset
  D_Flip_Flop d_ff_93 (.clk(and_11_out), .D(and_109_out), .Q(d_ff_93_q));  // open: Qn, preset, en, reset
  D_Flip_Flop d_ff_94 (.clk(and_11_out), .D(and_110_out), .Q(d_ff_94_q));  // open: Qn, preset, en, reset
  D_Flip_Flop d_ff_95 (.clk(and_11_out), .D(and_111_out), .Q(d_ff_95_q));  // open: Qn, preset, en, reset
  D_Flip_Flop d_ff_96 (.clk(and_11_out), .D(and_112_out), .Q(d_ff_96_q));  // open: Qn, preset, en, reset
  D_Flip_Flop d_ff_97 (.clk(and_12_out), .D(and_113_out), .Q(d_ff_97_q));  // open: Qn, preset, en, reset
  D_Flip_Flop d_ff_98 (.clk(and_12_out), .D(and_114_out), .Q(d_ff_98_q));  // open: Qn, preset, en, reset
  D_Flip_Flop d_ff_99 (.clk(and_12_out), .D(and_115_out), .Q(d_ff_99_q));  // open: Qn, preset, en, reset
  D_Flip_Flop d_ff_100 (.clk(and_116_out), .Q(d_ff_100_q));  // open: D, Qn, preset, en, reset
  D_Flip_Flop d_ff_101 (.clk(and_12_out), .D(and_117_out), .Q(d_ff_101_q));  // open: Qn, preset, en, reset
  D_Flip_Flop d_ff_102 (.clk(and_12_out), .D(and_118_out), .Q(d_ff_102_q));  // open: Qn, preset, en, reset
  D_Flip_Flop d_ff_103 (.clk(and_12_out), .D(and_119_out), .Q(d_ff_103_q));  // open: Qn, preset, en, reset
  D_Flip_Flop d_ff_104 (.clk(and_12_out), .D(and_120_out), .Q(d_ff_104_q));  // open: Qn, preset, en, reset
  D_Flip_Flop d_ff_105 (.clk(and_13_out), .D(and_121_out), .Q(d_ff_105_q));  // open: Qn, preset, en, reset
  D_Flip_Flop d_ff_106 (.clk(and_13_out), .D(and_122_out), .Q(d_ff_106_q));  // open: Qn, preset, en, reset
  D_Flip_Flop d_ff_107 (.clk(and_13_out), .D(and_123_out), .Q(d_ff_107_q));  // open: Qn, preset, en, reset
  D_Flip_Flop d_ff_108 (.clk(and_13_out), .D(and_124_out), .Q(d_ff_108_q));  // open: Qn, preset, en, reset
  D_Flip_Flop d_ff_109 (.clk(and_13_out), .D(and_125_out), .Q(d_ff_109_q));  // open: Qn, preset, en, reset
  D_Flip_Flop d_ff_110 (.clk(and_13_out), .D(and_126_out), .Q(d_ff_110_q));  // open: Qn, preset, en, reset
  D_Flip_Flop d_ff_111 (.clk(and_13_out), .D(and_127_out), .Q(d_ff_111_q));  // open: Qn, preset, en, reset
  D_Flip_Flop d_ff_112 (.clk(and_13_out), .D(and_128_out), .Q(d_ff_112_q));  // open: Qn, preset, en, reset
  D_Flip_Flop d_ff_113 (.clk(and_14_out), .D(and_129_out), .Q(d_ff_113_q));  // open: Qn, preset, en, reset
  D_Flip_Flop d_ff_114 (.clk(and_14_out), .D(and_130_out), .Q(d_ff_114_q));  // open: Qn, preset, en, reset
  D_Flip_Flop d_ff_115 (.clk(and_14_out), .D(and_131_out), .Q(d_ff_115_q));  // open: Qn, preset, en, reset
  D_Flip_Flop d_ff_116 (.clk(and_14_out), .D(and_132_out), .Q(d_ff_116_q));  // open: Qn, preset, en, reset
  D_Flip_Flop d_ff_117 (.clk(and_14_out), .D(and_133_out), .Q(d_ff_117_q));  // open: Qn, preset, en, reset
  D_Flip_Flop d_ff_118 (.clk(and_14_out), .D(and_134_out), .Q(d_ff_118_q));  // open: Qn, preset, en, reset
  D_Flip_Flop d_ff_119 (.clk(and_14_out), .D(and_135_out), .Q(d_ff_119_q));  // open: Qn, preset, en, reset
  D_Flip_Flop d_ff_120 (.clk(and_14_out), .D(and_136_out), .Q(d_ff_120_q));  // open: Qn, preset, en, reset
  D_Flip_Flop d_ff_121 (.clk(and_15_out), .D(and_137_out), .Q(d_ff_121_q));  // open: Qn, preset, en, reset
  D_Flip_Flop d_ff_122 (.clk(and_15_out), .D(and_138_out), .Q(d_ff_122_q));  // open: Qn, preset, en, reset
  D_Flip_Flop d_ff_123 (.clk(and_15_out), .D(and_139_out), .Q(d_ff_123_q));  // open: Qn, preset, en, reset
  D_Flip_Flop d_ff_124 (.clk(and_15_out), .D(and_140_out), .Q(d_ff_124_q));  // open: Qn, preset, en, reset
  D_Flip_Flop d_ff_125 (.clk(and_15_out), .D(and_141_out), .Q(d_ff_125_q));  // open: Qn, preset, en, reset
  D_Flip_Flop d_ff_126 (.clk(and_15_out), .D(and_142_out), .Q(d_ff_126_q));  // open: Qn, preset, en, reset
  D_Flip_Flop d_ff_127 (.clk(and_15_out), .D(and_143_out), .Q(d_ff_127_q));  // open: Qn, preset, en, reset
  D_Flip_Flop d_ff_128 (.clk(and_15_out), .D(and_144_out), .Q(d_ff_128_q));  // open: Qn, preset, en, reset
  and and_145 (and_145_out[0], W_0__R_1, decoder_1_out0, d_ff_1_q);
  and and_146 (and_145_out[1], W_0__R_1, decoder_1_out0, d_ff_2_q);
  and and_147 (and_145_out[2], W_0__R_1, decoder_1_out0, d_ff_3_q);
  and and_148 (and_145_out[3], W_0__R_1, decoder_1_out0, d_ff_4_q);
  and and_149 (and_145_out[4], W_0__R_1, decoder_1_out0, d_ff_5_q);
  and and_150 (and_145_out[5], W_0__R_1, decoder_1_out0, d_ff_6_q);
  and and_151 (and_145_out[6], W_0__R_1, decoder_1_out0, d_ff_7_q);
  and and_152 (and_145_out[7], W_0__R_1, decoder_1_out0, d_ff_8_q);
  and and_153 (and_153_out[0], W_0__R_1, decoder_1_out1, d_ff_9_q);
  and and_154 (and_153_out[1], W_0__R_1, decoder_1_out1, d_ff_10_q);
  and and_155 (and_153_out[2], W_0__R_1, decoder_1_out1, d_ff_11_q);
  and and_156 (and_153_out[3], W_0__R_1, decoder_1_out1, d_ff_12_q);
  and and_157 (and_153_out[4], W_0__R_1, decoder_1_out1, d_ff_13_q);
  and and_158 (and_153_out[5], W_0__R_1, decoder_1_out1, d_ff_14_q);
  and and_159 (and_153_out[6], W_0__R_1, decoder_1_out1, d_ff_15_q);
  and and_160 (and_153_out[7], W_0__R_1, decoder_1_out1, d_ff_16_q);
  and and_161 (and_161_out[0], W_0__R_1, decoder_1_out2, d_ff_17_q);
  and and_162 (and_161_out[1], W_0__R_1, decoder_1_out2, d_ff_18_q);
  and and_163 (and_161_out[2], W_0__R_1, decoder_1_out2, d_ff_19_q);
  and and_164 (and_161_out[3], W_0__R_1, decoder_1_out2, d_ff_20_q);
  and and_165 (and_161_out[4], W_0__R_1, decoder_1_out2, d_ff_21_q);
  and and_166 (and_161_out[5], W_0__R_1, decoder_1_out2, d_ff_22_q);
  and and_167 (and_161_out[6], W_0__R_1, decoder_1_out2, d_ff_23_q);
  and and_168 (and_161_out[7], W_0__R_1, decoder_1_out2, d_ff_24_q);
  and and_169 (and_169_out[0], W_0__R_1, decoder_1_out3, d_ff_25_q);
  and and_170 (and_169_out[1], W_0__R_1, decoder_1_out3, d_ff_26_q);
  and and_171 (and_169_out[2], W_0__R_1, d_ff_27_q, decoder_1_out3);
  and and_172 (and_169_out[3], W_0__R_1, d_ff_28_q, decoder_1_out3);
  and and_173 (and_169_out[4], W_0__R_1, d_ff_29_q, decoder_1_out3);
  and and_174 (and_169_out[5], decoder_1_out3, d_ff_30_q, W_0__R_1);
  and and_175 (and_169_out[6], decoder_1_out3, d_ff_31_q, W_0__R_1);
  and and_176 (and_169_out[7], W_0__R_1, decoder_1_out3, d_ff_32_q);
  and and_177 (and_177_out[0], decoder_1_out4, W_0__R_1, d_ff_33_q);
  and and_178 (and_177_out[1], W_0__R_1, decoder_1_out4, d_ff_34_q);
  and and_179 (and_177_out[2], W_0__R_1, decoder_1_out4, d_ff_35_q);
  and and_180 (and_177_out[3], W_0__R_1, decoder_1_out4, d_ff_36_q);
  and and_181 (and_177_out[4], W_0__R_1, decoder_1_out4, d_ff_37_q);
  and and_182 (and_177_out[5], W_0__R_1, decoder_1_out4, d_ff_38_q);
  and and_183 (and_177_out[6], W_0__R_1, d_ff_39_q, decoder_1_out4);
  and and_184 (and_177_out[7], W_0__R_1, d_ff_40_q, decoder_1_out4);
  and and_185 (and_185_out[0], W_0__R_1, decoder_1_out5, d_ff_41_q);
  and and_186 (and_185_out[1], decoder_1_out5, d_ff_42_q, W_0__R_1);
  and and_187 (and_185_out[2], decoder_1_out5, d_ff_43_q, W_0__R_1);
  and and_188 (and_185_out[3], decoder_1_out5, d_ff_44_q, W_0__R_1);
  and and_189 (and_185_out[4], W_0__R_1, d_ff_45_q, decoder_1_out5);
  and and_190 (and_185_out[5], W_0__R_1, d_ff_46_q, decoder_1_out5);
  and and_191 (and_185_out[6], W_0__R_1, d_ff_47_q, decoder_1_out5);
  and and_192 (and_185_out[7], W_0__R_1, d_ff_48_q, decoder_1_out5);
  and and_193 (and_193_out[0], W_0__R_1, decoder_1_out6, d_ff_49_q);
  and and_194 (and_193_out[1], W_0__R_1, decoder_1_out6, d_ff_50_q);
  and and_195 (and_193_out[2], W_0__R_1, decoder_1_out6, d_ff_51_q);
  and and_196 (and_193_out[3], W_0__R_1, d_ff_52_q, decoder_1_out6);
  and and_197 (and_193_out[4], W_0__R_1, d_ff_53_q, decoder_1_out6);
  and and_198 (and_193_out[5], W_0__R_1, d_ff_54_q, decoder_1_out6);
  and and_199 (and_193_out[6], W_0__R_1, d_ff_55_q, decoder_1_out6);
  and and_200 (and_193_out[7], W_0__R_1, d_ff_56_q, decoder_1_out6);
  and and_201 (and_201_out[0], W_0__R_1, decoder_1_out7, d_ff_57_q);
  and and_202 (and_201_out[1], W_0__R_1, decoder_1_out7, d_ff_58_q);
  and and_203 (and_201_out[2], W_0__R_1, decoder_1_out7, d_ff_59_q);
  and and_204 (and_201_out[3], W_0__R_1, decoder_1_out7, d_ff_60_q);
  and and_205 (and_201_out[4], W_0__R_1, decoder_1_out7, d_ff_61_q);
  and and_206 (and_201_out[5], W_0__R_1, decoder_1_out7, d_ff_62_q);
  and and_207 (and_201_out[6], W_0__R_1, decoder_1_out7, d_ff_63_q);
  and and_208 (and_201_out[7], W_0__R_1, decoder_1_out7, d_ff_64_q);
  and and_209 (and_209_out[0], W_0__R_1, decoder_1_out8, d_ff_65_q);
  and and_210 (and_209_out[1], decoder_1_out8, d_ff_66_q, W_0__R_1);
  and and_211 (and_209_out[2], decoder_1_out8, d_ff_67_q, W_0__R_1);
  and and_212 (and_209_out[3], decoder_1_out8, d_ff_68_q, W_0__R_1);
  and and_213 (and_209_out[4], decoder_1_out8, d_ff_69_q, W_0__R_1);
  and and_214 (and_209_out[5], decoder_1_out8, d_ff_70_q, W_0__R_1);
  and and_215 (and_209_out[6], decoder_1_out8, d_ff_71_q, W_0__R_1);
  and and_216 (and_209_out[7], decoder_1_out8, d_ff_72_q, W_0__R_1);
  and and_217 (and_217_out[0], W_0__R_1, decoder_1_out9, d_ff_73_q);
  and and_218 (and_217_out[1], W_0__R_1, decoder_1_out9, d_ff_74_q);
  and and_219 (and_217_out[2], W_0__R_1, d_ff_75_q, decoder_1_out9);
  and and_220 (and_217_out[3], W_0__R_1, d_ff_76_q, decoder_1_out9);
  and and_221 (and_217_out[4], W_0__R_1, d_ff_77_q, decoder_1_out9);
  and and_222 (and_217_out[5], W_0__R_1, d_ff_78_q, decoder_1_out9);
  and and_223 (and_217_out[6], W_0__R_1, d_ff_79_q, decoder_1_out9, decoder_1_out9);
  and and_224 (and_217_out[7], W_0__R_1, d_ff_80_q, decoder_1_out9);
  and and_225 (and_225_out[0], W_0__R_1, decoder_1_out10, d_ff_81_q);
  and and_226 (and_225_out[1], W_0__R_1, decoder_1_out10, d_ff_82_q);
  and and_227 (and_225_out[2], W_0__R_1, decoder_1_out10, d_ff_83_q);
  and and_228 (and_225_out[3], W_0__R_1, decoder_1_out10, d_ff_84_q);
  and and_229 (and_225_out[4], W_0__R_1, decoder_1_out10, d_ff_85_q);
  and and_230 (and_225_out[5], W_0__R_1, decoder_1_out10, d_ff_86_q);
  and and_231 (and_225_out[6], W_0__R_1, decoder_1_out10, d_ff_87_q);
  and and_232 (and_225_out[7], W_0__R_1, d_ff_88_q, decoder_1_out10);
  and and_233 (and_233_out[0], W_0__R_1, decoder_1_out11, d_ff_89_q);
  and and_234 (and_233_out[1], W_0__R_1, decoder_1_out11, d_ff_90_q);
  and and_235 (and_233_out[2], W_0__R_1, decoder_1_out11, d_ff_91_q);
  and and_236 (and_233_out[3], W_0__R_1, decoder_1_out11, d_ff_92_q);
  and and_237 (and_233_out[4], W_0__R_1, decoder_1_out11, d_ff_93_q);
  and and_238 (and_233_out[5], W_0__R_1, decoder_1_out11, d_ff_94_q);
  and and_239 (and_233_out[6], W_0__R_1, decoder_1_out11, d_ff_95_q);
  and and_240 (and_233_out[7], W_0__R_1, decoder_1_out11, d_ff_96_q);
  and and_241 (and_241_out[0], W_0__R_1, decoder_1_out12, d_ff_97_q);
  and and_242 (and_241_out[1], W_0__R_1, decoder_1_out12, d_ff_98_q);
  and and_243 (and_241_out[2], W_0__R_1, decoder_1_out12, d_ff_99_q);
  and and_244 (and_241_out[3], W_0__R_1, decoder_1_out12, d_ff_100_q);
  and and_245 (and_241_out[4], W_0__R_1, decoder_1_out12, d_ff_101_q);
  and and_246 (and_241_out[5], W_0__R_1, decoder_1_out12, d_ff_102_q);
  and and_247 (and_241_out[6], W_0__R_1, decoder_1_out12, d_ff_103_q);
  and and_248 (and_241_out[7], W_0__R_1, decoder_1_out12, d_ff_104_q);
  and and_249 (and_249_out[0], W_0__R_1, decoder_1_out13, d_ff_105_q);
  and and_250 (and_249_out[1], W_0__R_1, decoder_1_out13, d_ff_106_q);
  and and_251 (and_249_out[2], decoder_1_out13, d_ff_107_q);
  and and_252 (and_249_out[3], W_0__R_1, d_ff_108_q, decoder_1_out13);
  and and_253 (and_249_out[4], decoder_1_out13, d_ff_109_q, W_0__R_1);
  and and_254 (and_249_out[5], decoder_1_out13, d_ff_110_q, W_0__R_1);
  and and_255 (and_249_out[6], decoder_1_out13, d_ff_111_q, W_0__R_1);
  and and_256 (and_249_out[7], decoder_1_out13, d_ff_112_q, W_0__R_1);
  and and_257 (and_257_out[0], W_0__R_1, decoder_1_out14, d_ff_113_q);
  and and_258 (and_257_out[1], W_0__R_1, decoder_1_out14, d_ff_114_q);
  and and_259 (and_257_out[2], W_0__R_1, d_ff_115_q, decoder_1_out14);
  and and_260 (and_257_out[3], W_0__R_1, d_ff_116_q, decoder_1_out14);
  and and_261 (and_257_out[4], W_0__R_1, d_ff_117_q, decoder_1_out14);
  and and_262 (and_257_out[5], W_0__R_1, d_ff_118_q, decoder_1_out14);
  and and_263 (and_257_out[6], W_0__R_1, d_ff_119_q, decoder_1_out14);
  and and_264 (and_257_out[7], W_0__R_1, d_ff_120_q, decoder_1_out14);
  and and_265 (and_265_out[0], W_0__R_1, decoder_1_out15, d_ff_121_q);
  and and_266 (and_265_out[1], W_0__R_1, d_ff_122_q, decoder_1_out15);
  and and_267 (and_265_out[2], W_0__R_1, d_ff_123_q, decoder_1_out15);
  and and_268 (and_265_out[3], W_0__R_1, d_ff_124_q, decoder_1_out15);
  and and_269 (and_265_out[4], W_0__R_1, d_ff_125_q, decoder_1_out15);
  and and_270 (and_265_out[5], W_0__R_1, d_ff_126_q, decoder_1_out15);
  and and_271 (and_265_out[6], W_0__R_1, d_ff_127_q, decoder_1_out15);
  and and_272 (and_265_out[7], W_0__R_1, d_ff_128_q, decoder_1_out15);
  Multiplexer #(.select(4), .width(8)) multiplexer_1 (
    .in0(and_145_out), .in1(and_153_out), .in2(and_161_out), .in3(and_169_out), .in4(and_177_out),
    .in5(and_185_out), .in6(and_193_out), .in7(and_201_out), .in8(and_209_out), .in9(and_217_out),
    .in10(and_225_out), .in11(and_233_out), .in12(and_241_out), .in13(and_249_out), .in14(and_257_out),
    .in15(and_265_out), .out({_7_2, _6_2, _5_2, _4_2, _3_2, _2_2, _1_2, _0_2}), .sel(Add__Nibble));  // open: en

  // Notes on the sheet:
  //   adress
  //   Clk
  //   read/write
  //   data
endmodule

module _8_bit_Register (
  input  [7:0] Input_Byte,
  input  Clock,
  output [7:0] Output_Byte
);

  D_Flip_Flop d_ff_1 (.clk(Clock), .D(Input_Byte[0]), .Q(Output_Byte[0]));  // open: Qn, preset, en, reset
  D_Flip_Flop d_ff_2 (.clk(Clock), .D(Input_Byte[1]), .Q(Output_Byte[1]));  // open: Qn, preset, en, reset
  D_Flip_Flop d_ff_3 (.clk(Clock), .D(Input_Byte[2]), .Q(Output_Byte[2]));  // open: Qn, preset, en, reset
  D_Flip_Flop d_ff_4 (.clk(Clock), .D(Input_Byte[3]), .Q(Output_Byte[3]));  // open: Qn, preset, en, reset
  D_Flip_Flop d_ff_5 (.clk(Clock), .D(Input_Byte[4]), .Q(Output_Byte[4]));  // open: Qn, preset, en, reset
  D_Flip_Flop d_ff_6 (.clk(Clock), .D(Input_Byte[5]), .Q(Output_Byte[5]));  // open: Qn, preset, en, reset
  D_Flip_Flop d_ff_7 (.clk(Clock), .D(Input_Byte[6]), .Q(Output_Byte[6]));  // open: Qn, preset, en, reset
  D_Flip_Flop d_ff_8 (.clk(Clock), .D(Input_Byte[7]), .Q(Output_Byte[7]));  // open: Qn, preset, en, reset

  // Notes on the sheet:
  //   Input
  //   Clock
  //   8-bit Register
  //   Output
endmodule

module _4_bit_Register (
  input  [3:0] Input_Nibble,
  input  Clock,
  output [3:0] Output_Nibble
);

  D_Flip_Flop d_ff_1 (.clk(Clock), .D(Input_Nibble[0]), .Q(Output_Nibble[0]));  // open: Qn, preset, en, reset
  D_Flip_Flop d_ff_2 (.clk(Clock), .D(Input_Nibble[1]), .Q(Output_Nibble[1]));  // open: Qn, preset, en, reset
  D_Flip_Flop d_ff_3 (.clk(Clock), .D(Input_Nibble[2]), .Q(Output_Nibble[2]));  // open: Qn, preset, en, reset
  D_Flip_Flop d_ff_4 (.clk(Clock), .D(Input_Nibble[3]), .Q(Output_Nibble[3]));  // open: Qn, preset, en, reset

  // Notes on the sheet:
  //   Input
  //   Clock
  //   4-bit Register
  //   Output
endmodule

module ALU (
  input  [7:0] INPUT,
  input  Clock,
  input  _0_R__1_L,
  input  Enable,
  input  ANS_Enable,
  input  _0_ADD__1_SUB,
  output [7:0] Byte_Out,
  output Overflow,
  output Negative,
  output Zero
);

  wire and_3_out, and_4_out, and_6_out, demultiplexer_1_out0, demultiplexer_1_out1, not_3_out, not_4_out,
       or_2_out, xor_1_out, xor_2_out;
  wire [7:0] adder_1_out, adder_2_out, and_1_out, and_2_out, n8_bit_register_1_output_byte,
       n8_bit_register_2_output_byte, not_1_out, not_2_out, not_5_out, or_1_out;

  Demultiplexer demultiplexer_1 (
    .out0(demultiplexer_1_out0), .out1(demultiplexer_1_out1), .in(Clock), .sel(Enable), .en(_0_R__1_L));
  _8_bit_Register u_8_bit_register_1 (
    .Input_Byte(INPUT), .Clock(demultiplexer_1_out0), .Output_Byte(n8_bit_register_1_output_byte));
  _8_bit_Register u_8_bit_register_2 (
    .Input_Byte(INPUT), .Clock(demultiplexer_1_out1), .Output_Byte(n8_bit_register_2_output_byte));
  assign not_1_out = ~{8{_0_ADD__1_SUB}};  // NOT_Gate not_1, 8 bits wide
  assign and_1_out = n8_bit_register_2_output_byte & not_1_out;  // AND_Gate and_1, 8 bits wide
  assign and_2_out = n8_bit_register_2_output_byte & {8{_0_ADD__1_SUB}};  // AND_Gate and_2, 8 bits wide
  assign not_2_out = ~and_2_out;  // NOT_Gate not_2, 8 bits wide
  Adder adder_1 (.a(8'h1), .b(not_2_out), .out(adder_1_out));  // open: cin, cout
  assign or_1_out = and_1_out | adder_1_out;  // OR_Gate or_1, 8 bits wide
  and and_3 (and_3_out, and_1_out[7], not_3_out);
  not not_3 (not_3_out, _0_ADD__1_SUB);
  and and_4 (and_4_out, adder_1_out[7], _0_ADD__1_SUB);
  or or_2 (or_2_out, and_3_out, and_4_out);
  Adder adder_2 (.a(n8_bit_register_1_output_byte), .b(or_1_out), .out(adder_2_out));  // open: cin, cout
  not not_4 (not_4_out, xor_1_out);
  xor xor_1 (xor_1_out, n8_bit_register_1_output_byte[7], or_2_out);
  xor xor_2 (xor_2_out, adder_2_out[7], n8_bit_register_1_output_byte[7]);
  and and_5 (Overflow, xor_2_out, not_4_out);
  and and_6 (and_6_out, Clock, ANS_Enable);
  assign not_5_out = ~Byte_Out;  // NOT_Gate not_5, 8 bits wide
  and and_7 (Zero, not_5_out[7], not_5_out[6], not_5_out[5], not_5_out[4], not_5_out[3], not_5_out[2], not_5_out[1], not_5_out[0]);
  not not_6 (Negative, not_5_out[7]);
  _8_bit_Register u_8_bit_register_3 (.Input_Byte(adder_2_out), .Clock(and_6_out), .Output_Byte(Byte_Out));

  // Notes on the sheet:
  //   Operation from CU
  //   R
  //   L
  //   Extend to Byte
  //   Constant 1
  //   2's Complement
  //   Adder
  //   Overflow Checker
  //   Neg. Flag
  //   Zero Checker
  //   A Reg.
endmodule

module STATUS_Register (
  input  Overflow,
  input  Negative,
  input  Zero,
  input  Clock,
  output Overflow_2,
  output Negative_2,
  output Zero_2
);

  D_Flip_Flop d_ff_1 (.clk(Clock), .D(Overflow), .Q(Overflow_2));  // open: Qn, preset, en, reset
  D_Flip_Flop d_ff_2 (.clk(Clock), .D(Negative), .Q(Negative_2));  // open: Qn, preset, en, reset
  D_Flip_Flop d_ff_3 (.clk(Clock), .D(Zero), .Q(Zero_2));  // open: Qn, preset, en, reset
endmodule

module Binary_to_BCD (
  input  [7:0] in_1,
  output [3:0] H,
  output [3:0] T,
  output [3:0] O
);

  wire add3_1_out_5, add3_1_out_6, add3_1_out_7, add3_1_out_8, add3_2_out_5, add3_2_out_6, add3_2_out_7,
       add3_2_out_8, add3_3_out_5, add3_3_out_6, add3_3_out_7, add3_3_out_8, add3_4_out_6, add3_4_out_7,
       add3_4_out_8, add3_6_out_5, add3_6_out_6, add3_6_out_7, add3_6_out_8;

  add3 add3_1 (
    .msb(1'b0), .in_2(in_1[7]), .in_3(in_1[6]), .lsb(in_1[5]), .out_5(add3_1_out_5), .out_6(add3_1_out_6),
    .out_7(add3_1_out_7), .out_8(add3_1_out_8));
  add3 add3_2 (
    .msb(add3_1_out_6), .in_2(add3_1_out_7), .in_3(add3_1_out_8), .lsb(in_1[4]), .out_5(add3_2_out_5),
    .out_6(add3_2_out_6), .out_7(add3_2_out_7), .out_8(add3_2_out_8));
  add3 add3_3 (
    .msb(add3_2_out_6), .in_2(add3_2_out_7), .in_3(add3_2_out_8), .lsb(in_1[3]), .out_5(add3_3_out_5),
    .out_6(add3_3_out_6), .out_7(add3_3_out_7), .out_8(add3_3_out_8));
  add3 add3_4 (
    .msb(1'b0), .in_2(add3_1_out_5), .in_3(add3_2_out_5), .lsb(add3_3_out_5), .out_5(H[1]),
    .out_6(add3_4_out_6), .out_7(add3_4_out_7), .out_8(add3_4_out_8));
  add3 add3_5 (
    .msb(add3_4_out_6), .in_2(add3_4_out_7), .in_3(add3_4_out_8), .lsb(add3_6_out_5), .out_5(H[0]),
    .out_6(T[3]), .out_7(T[2]), .out_8(T[1]));
  add3 add3_6 (
    .msb(add3_3_out_6), .in_2(add3_3_out_7), .in_3(add3_3_out_8), .lsb(in_1[2]), .out_5(add3_6_out_5),
    .out_6(add3_6_out_6), .out_7(add3_6_out_7), .out_8(add3_6_out_8));
  add3 add3_7 (
    .msb(add3_6_out_6), .in_2(add3_6_out_7), .in_3(add3_6_out_8), .lsb(in_1[1]), .out_5(T[0]), .out_6(O[3]),
    .out_7(O[2]), .out_8(O[1]));

  assign H[3:2] = 2'b00;
  assign O[0] = in_1[0];
endmodule

module add3 (
  input  msb,
  input  in_2,
  input  in_3,
  input  lsb,
  output out_5,
  output out_6,
  output out_7,
  output out_8
);

  wire and_1_out, and_2_out, and_3_out, and_4_out, and_5_out, and_6_out, and_7_out, and_8_out, and_9_out,
       not_1_out, not_2_out, not_3_out, not_4_out, not_5_out, not_6_out, not_7_out, not_8_out, not_9_out,
       not_10_out, not_11_out, not_12_out, not_13_out, not_14_out, not_15_out, not_16_out, not_17_out,
       not_18_out, not_19_out, not_20_out, not_21_out;

  not not_1 (not_1_out, in_3);
  not not_2 (not_2_out, in_2);
  not not_3 (not_3_out, msb);
  not not_4 (not_4_out, lsb);
  not not_5 (not_5_out, in_2);
  not not_6 (not_6_out, msb);
  not not_7 (not_7_out, in_2);
  not not_8 (not_8_out, msb);
  not not_9 (not_9_out, lsb);
  not not_10 (not_10_out, in_3);
  not not_11 (not_11_out, msb);
  not not_12 (not_12_out, in_3);
  not not_13 (not_13_out, msb);
  not not_14 (not_14_out, lsb);
  not not_15 (not_15_out, msb);
  not not_16 (not_16_out, msb);
  not not_17 (not_17_out, lsb);
  not not_18 (not_18_out, in_3);
  not not_19 (not_19_out, in_2);
  not not_20 (not_20_out, in_3);
  not not_21 (not_21_out, in_2);
  and and_1 (and_1_out, lsb, not_1_out, not_2_out, not_3_out);
  and and_2 (and_2_out, not_4_out, in_3, not_5_out, not_6_out);
  and and_3 (and_3_out, lsb, in_3, not_7_out, not_8_out);
  and and_4 (and_4_out, not_9_out, not_10_out, in_2, not_11_out);
  and and_5 (and_5_out, lsb, not_12_out, in_2, not_13_out);
  and and_6 (and_6_out, not_14_out, in_3, in_2, not_15_out);
  and and_7 (and_7_out, lsb, in_3, in_2, not_16_out);
  and and_8 (and_8_out, not_17_out, not_18_out, not_19_out, msb);
  and and_9 (and_9_out, lsb, not_20_out, not_21_out, msb);
  or or_1 (out_8, and_3_out, and_1_out, and_6_out, and_8_out);
  or or_2 (out_7, and_2_out, and_3_out, and_7_out, and_8_out);
  or or_3 (out_6, and_9_out, and_4_out);
  or or_4 (out_5, and_9_out, and_8_out, and_6_out, and_5_out, and_7_out);
endmodule

module BCDtoDigit (
  input  [3:0] in_1,
  output right_up,
  output up,
  output left_up,
  output mid,
  output leftdown,
  output down,
  output right_down
);

  wire _0_out, _1_out, _2_out, _3_out, _4_out, _5_out, _6_out, _7_out, _8_out, _9_out, not_1_out, not_2_out,
       not_3_out, not_4_out;

  not not_1 (not_1_out, in_1[3]);
  not not_2 (not_2_out, in_1[2]);
  not not_3 (not_3_out, in_1[0]);
  not not_4 (not_4_out, in_1[1]);
  and _1 (_1_out, in_1[0], not_4_out, not_2_out, not_1_out);
  and _2 (_2_out, not_3_out, in_1[1], not_2_out, not_1_out);
  and _3 (_3_out, in_1[0], in_1[1], not_2_out, not_1_out);
  and _4 (_4_out, not_3_out, not_4_out, in_1[2], not_1_out);
  and _5 (_5_out, in_1[0], not_4_out, in_1[2], not_1_out);
  and _6 (_6_out, not_3_out, in_1[1], in_1[2], not_1_out);
  and _7 (_7_out, in_1[0], in_1[1], in_1[2], not_1_out);
  and _8 (_8_out, not_3_out, not_4_out, not_2_out, in_1[3]);
  and _9 (_9_out, in_1[0], not_4_out, not_2_out, in_1[3]);
  and _0 (_0_out, not_3_out, not_4_out, not_2_out, not_1_out);
  or or_1 (right_up, _1_out, _2_out, _3_out, _4_out, _7_out, _8_out, _9_out, _0_out);
  or or_2 (up, _2_out, _3_out, _5_out, _6_out, _7_out, _8_out, _9_out, _0_out);
  or or_3 (left_up, _4_out, _5_out, _6_out, _8_out, _9_out, _0_out);
  or or_4 (mid, _2_out, _3_out, _4_out, _6_out, _5_out, _8_out, _9_out);
  or or_5 (leftdown, _2_out, _6_out, _8_out, _0_out);
  or or_6 (down, _8_out, _2_out, _3_out, _5_out, _6_out, _0_out);
  or or_7 (right_down, _1_out, _3_out, _4_out, _5_out, _0_out, _6_out, _7_out, _8_out, _9_out);
endmodule

module InputtoBinary (
  input  _0,
  input  _1,
  input  _2,
  input  _3,
  input  _4,
  input  _5,
  input  _6,
  input  _7,
  input  _8,
  input  _9,
  output [3:0] out_11
);

  or or_1 (out_11[0], _1, _3, _5, _7, _9);
  or or_2 (out_11[1], _2, _6, _3, _7);
  or or_3 (out_11[2], _4, _5, _6, _7);
  or or_4 (out_11[3], _8, _9);
endmodule

module Cu_T1 (
  input  [7:0] in_1,
  input  in_2,
  input  in_3,
  input  in_4,
  output _0,
  output out_6,
  output out_7,
  output _4,
  output LD_R1,
  output LD_R2,
  output STR_R1,
  output STR_R2,
  output ADD_R1,
  output ADD_R2,
  output SUB_R1,
  output SUB_R2,
  output BEQ,
  output BNQ,
  output PRT_R1,
  output PRT_R2,
  output INP_R1,
  output INP_R2,
  output STOP,
  output CLEAR,
  output MBR_in_1_out__0,
  output PC_MAR,
  output RAM_DR_in_1_out__0,
  output Ri_in_1_out__0,
  output input_get__1
);

  wire d_ff_2_qn, d_ff_3_qn, d_ff_4_qn, d_ff_5_qn, d_ff_7_qn, d_ff_8_qn, d_ff_9_qn, d_ff_10_qn, d_ff_11_qn,
       d_ff_12_qn, d_ff_14_qn, d_ff_15_qn, j_k_ff_1_q, j_k_ff_2_q, j_k_ff_3_q, j_k_ff_4_q, not_1_out,
       not_2_out, not_3_out, not_4_out;

  J_K_Flip_Flop j_k_ff_1 (.J(in_3), .clk(in_2), .K(in_4), .Q(j_k_ff_1_q));  // open: Qn, preset, en, reset
  not not_1 (not_1_out, in_1[6]);
  not not_2 (not_2_out, in_1[7]);
  J_K_Flip_Flop j_k_ff_2 (.J(in_3), .clk(j_k_ff_1_q), .K(in_4), .Q(j_k_ff_2_q));  // open: Qn, preset, en, reset
  not not_3 (not_3_out, in_1[4]);
  not not_4 (not_4_out, in_1[5]);
  J_K_Flip_Flop j_k_ff_3 (.J(in_3), .clk(j_k_ff_2_q), .K(in_4), .Q(j_k_ff_3_q));  // open: Qn, preset, en, reset
  J_K_Flip_Flop j_k_ff_4 (.J(in_3), .clk(j_k_ff_3_q), .K(in_4), .Q(j_k_ff_4_q));  // open: Qn, preset, en, reset
  and and_1 (LD_R1, not_3_out, in_1[5], not_1_out, not_2_out);
  and and_2 (LD_R2, in_1[4], in_1[5], not_1_out, not_2_out);
  and and_3 (STR_R1, not_3_out, not_4_out, in_1[6], not_2_out);
  and and_4 (STR_R2, in_1[4], not_4_out, in_1[6], not_2_out);
  and and_5 (ADD_R1, not_3_out, not_4_out, not_1_out, in_1[7]);
  and and_6 (ADD_R2, in_1[4], not_4_out, not_1_out, in_1[7]);
  and and_7 (SUB_R1, not_3_out, not_4_out, in_1[6], in_1[7]);
  and and_8 (SUB_R2, in_1[4], not_4_out, in_1[6], in_1[7]);
  and and_9 (BEQ, not_3_out, in_1[5], in_1[6], not_2_out);
  and and_10 (BNQ, in_1[4], in_1[5], in_1[6], not_2_out);
  and and_11 (PRT_R1, not_3_out, in_1[5], not_1_out, in_1[7]);
  and and_12 (PRT_R2, in_1[4], in_1[5], not_1_out, in_1[7]);
  and and_13 (INP_R1, not_3_out, in_1[5], in_1[6], in_1[7]);
  and and_14 (INP_R2, in_1[4], in_1[5], in_1[6], in_1[7]);
  and and_15 (STOP, not_3_out, not_4_out, not_1_out, not_2_out);
  and and_16 (CLEAR, in_1[4], not_4_out, not_1_out, not_2_out);
  D_Flip_Flop d_ff_1 (.clk(in_2));  // open: D, Q, Qn, preset, en, reset
  D_Flip_Flop d_ff_2 (.clk(in_2), .Qn(d_ff_2_qn));  // open: D, Q, preset, en, reset
  D_Flip_Flop d_ff_3 (.clk(in_2), .Qn(d_ff_3_qn));  // open: D, Q, preset, en, reset
  D_Flip_Flop d_ff_4 (.clk(in_2), .Qn(d_ff_4_qn));  // open: D, Q, preset, en, reset
  D_Flip_Flop d_ff_5 (.clk(in_2), .Qn(d_ff_5_qn));  // open: D, Q, preset, en, reset
  D_Flip_Flop d_ff_6 (.clk(in_2), .D(d_ff_2_qn));  // open: Q, Qn, preset, en, reset
  D_Flip_Flop d_ff_7 (.clk(in_2), .D(d_ff_3_qn), .Qn(d_ff_7_qn));  // open: Q, preset, en, reset
  D_Flip_Flop d_ff_8 (.clk(in_2), .D(d_ff_4_qn), .Qn(d_ff_8_qn));  // open: Q, preset, en, reset
  D_Flip_Flop d_ff_9 (.clk(in_2), .D(d_ff_5_qn), .Qn(d_ff_9_qn));  // open: Q, preset, en, reset
  D_Flip_Flop d_ff_10 (.clk(in_2), .D(d_ff_7_qn), .Qn(d_ff_10_qn));  // open: Q, preset, en, reset
  D_Flip_Flop d_ff_11 (.clk(in_2), .D(d_ff_8_qn), .Qn(d_ff_11_qn));  // open: Q, preset, en, reset
  D_Flip_Flop d_ff_12 (.clk(in_2), .D(d_ff_9_qn), .Qn(d_ff_12_qn));  // open: Q, preset, en, reset
  D_Flip_Flop d_ff_13 (.clk(in_2), .D(d_ff_11_qn));  // open: Q, Qn, preset, en, reset
  D_Flip_Flop d_ff_14 (.clk(in_2), .D(d_ff_12_qn), .Qn(d_ff_14_qn));  // open: Q, preset, en, reset
  D_Flip_Flop d_ff_15 (.clk(in_2), .D(d_ff_14_qn), .Qn(d_ff_15_qn));  // open: Q, preset, en, reset

  assign _0 = in_1[0];
  assign _4 = in_1[3];
  assign out_6 = in_1[1];
  assign out_7 = in_1[2];

  // Notes on the sheet:
  //   STOP: 0000
  //   Free 0001
  //   LD :0010 ADDR -> R1
  //   LD :0011 ADDR -> R2
  //   STR :0100 ADDR <- R1
  //   STR :0101 ADDR <- R2
  //   ADD: 1000 R1 + R2 -> R1
  //   ADD: 1001 R1 + R2 -> R2
  //   SUB: 1100 R1 - R2 -> R1
  //   SUB: 1101 R2-R1 -> R2
  //   BEQ: 0110 ADDR
  //   BNQ 0111 ADDR
  //   PRT: 1010 Print R1
  //   PRT: 1011 Print R2
  //   INP: 1110 input -> R1
  //   INP: 1111 input -> R2
endmodule

module Pulse (
  input  Clk,
  input  in,
  output out_3
);

  wire j_k_ff_1_q, xor_1_out;

  ExactlyOne xor_1 (.out(xor_1_out), .in1(j_k_ff_1_q), .in2(in), .in3(out_3));
  D_Flip_Flop d_ff_1 (.clk(Clk), .D(xor_1_out), .Q(out_3));  // open: Qn, preset, en, reset
  J_K_Flip_Flop j_k_ff_1 (.J(out_3), .clk(Clk), .K(out_3), .Q(j_k_ff_1_q));  // open: Qn, preset, en, reset
endmodule

module Multiplier (
  input  [7:0] number,
  input  [7:0] multiplier,
  output [13:0] out_3
);

  wire adder_6_cout;
  wire [6:0] and_38_out;
  wire [7:1] and_41_out;
  wire [8:2] and_42_out;
  wire [9:3] and_44_out;
  wire [10:4] and_47_out;
  wire [11:5] and_48_out;
  wire [12:6] and_49_out;
  wire [13:0] adder_1_out, adder_2_out, adder_3_out, adder_4_out, adder_5_out;

  and and_1 (and_49_out[12], number[6], multiplier[6]);
  and and_2 (and_38_out[6], number[6], multiplier[0]);
  and and_3 (and_41_out[6], number[5], multiplier[1]);
  and and_4 (and_41_out[7], number[6], multiplier[1]);
  and and_5 (and_42_out[8], number[6], multiplier[2]);
  and and_6 (and_42_out[7], number[5], multiplier[2]);
  and and_7 (and_44_out[9], number[6], multiplier[3]);
  and and_8 (and_44_out[8], number[5], multiplier[3]);
  and and_9 (and_47_out[9], number[5], multiplier[4]);
  and and_10 (and_47_out[8], number[4], multiplier[4]);
  and and_11 (and_47_out[10], number[6], multiplier[4]);
  and and_12 (and_48_out[11], number[6], multiplier[5]);
  and and_13 (and_48_out[9], number[4], multiplier[5]);
  and and_14 (and_48_out[10], number[5], multiplier[5]);
  and and_15 (and_49_out[10], number[4], multiplier[6]);
  and and_16 (and_49_out[11], number[5], multiplier[6]);
  and and_17 (and_38_out[3], number[3], multiplier[0]);
  and and_18 (and_38_out[5], number[5], multiplier[0]);
  and and_19 (and_38_out[4], number[4], multiplier[0]);
  and and_20 (and_41_out[4], number[3], multiplier[1]);
  and and_21 (and_41_out[5], number[4], multiplier[1]);
  and and_22 (and_42_out[4], number[2], multiplier[2]);
  and and_23 (and_42_out[6], number[4], multiplier[2]);
  and and_24 (and_42_out[5], number[3], multiplier[2]);
  and and_25 (and_44_out[6], number[3], multiplier[3]);
  and and_26 (and_44_out[5], number[2], multiplier[3]);
  and and_27 (and_44_out[7], number[4], multiplier[3]);
  and and_28 (and_47_out[7], number[3], multiplier[4]);
  and and_29 (and_47_out[6], number[2], multiplier[4]);
  and and_30 (and_48_out[6], number[1], multiplier[5]);
  and and_31 (and_48_out[7], number[2], multiplier[5]);
  and and_32 (and_48_out[8], number[3], multiplier[5]);
  and and_33 (and_49_out[9], number[3], multiplier[6]);
  and and_34 (and_49_out[7], number[1], multiplier[6]);
  and and_35 (and_49_out[8], number[2], multiplier[6]);
  and and_36 (and_38_out[2], number[2], multiplier[0]);
  and and_37 (and_38_out[1], number[1], multiplier[0]);
  and and_38 (and_38_out[0], number[0], multiplier[0]);
  and and_39 (and_41_out[2], number[1], multiplier[1]);
  and and_40 (and_41_out[3], number[2], multiplier[1]);
  and and_41 (and_41_out[1], number[0], multiplier[1]);
  and and_42 (and_42_out[2], number[0], multiplier[2]);
  and and_43 (and_42_out[3], number[1], multiplier[2]);
  and and_44 (and_44_out[3], number[0], multiplier[3]);
  and and_45 (and_44_out[4], number[1], multiplier[3]);
  and and_46 (and_47_out[5], number[1], multiplier[4]);
  and and_47 (and_47_out[4], number[0], multiplier[4]);
  and and_48 (and_48_out[5], number[0], multiplier[5]);
  and and_49 (and_49_out[6], number[0], multiplier[6]);
  Adder #(.width(14)) adder_1 (
    .a({{7{1'b0}}, and_38_out}), .b({{6{1'b0}}, and_41_out, 1'b0}), .out(adder_1_out));  // open: cin, cout
  Adder #(.width(14)) adder_2 (
    .a(adder_1_out), .b({{5{1'b0}}, and_42_out, 2'b00}), .out(adder_2_out));  // open: cin, cout
  Adder #(.width(14)) adder_3 (
    .a(adder_2_out), .b({4'b0000, and_44_out, 3'b000}), .out(adder_3_out));  // open: cin, cout
  Adder #(.width(14)) adder_4 (
    .a(adder_3_out), .b({3'b000, and_47_out, 4'b0000}), .out(adder_4_out));  // open: cin, cout
  Adder #(.width(14)) adder_5 (
    .a(adder_4_out), .b({2'b00, and_48_out, {5{1'b0}}}), .out(adder_5_out));  // open: cin, cout
  Adder #(.width(14)) adder_6 (
    .a(adder_5_out), .b({1'b0, and_49_out, {6{1'b0}}}), .out(out_3), .cout(adder_6_cout));  // open: cin

  // Notes on the sheet:
  //   X
endmodule
